// Logisim project latch_and_flip_flop_and_ic.circ as structural Verilog
module SR_Latch_Active_High (
  input  R,
  input  S,
  output Q,
  output Q_prime
);

  nor nor_1 (Q, R, Q_prime);
  nor nor_2 (Q_prime, Q, S);
endmodule

module SR_Latch_Active_Low (
  input  S,
  input  R,
  output Q,
  output Q_prime
);

  nand nand_1 (Q, S, Q_prime);
  nand nand_2 (Q_prime, Q, R);
endmodule

module Gated_SR_Latch_Active_High_With_NOR (
  input  R,
  input  E,
  input  S,
  output Q,
  output Q_prime
);

  wire and_1_out, and_2_out;

  and and_1 (and_1_out, R, E);
  and and_2 (and_2_out, E, S);
  nor nor_1 (Q, and_1_out, Q_prime);
  nor nor_2 (Q_prime, Q, and_2_out);
endmodule

module Gated_SR_Latch_Active_High_With_NAND (
  input  S,
  input  E,
  input  R,
  output Q,
  output Q_prime
);

  wire nand_1_out, nand_2_out;

  nand nand_1 (nand_1_out, S, E);
  nand nand_2 (nand_2_out, E, R);
  nand nand_3 (Q, nand_1_out, Q_prime);
  nand nand_4 (Q_prime, Q, nand_2_out);
endmodule

module Gated_D_Latch_Active_High_With_NOR (
  input  E,
  input  D,
  output Q,
  output Q_prime
);

  wire and_1_out, and_2_out, not_1_out;

  not not_1 (not_1_out, D);
  and and_1 (and_1_out, not_1_out, E);
  and and_2 (and_2_out, E, D);
  nor nor_1 (Q, and_1_out, Q_prime);
  nor nor_2 (Q_prime, Q, and_2_out);
endmodule

module Gated_D_Latch_Active_High_With_NAND (
  input  D,
  input  E,
  output Q,
  output Q_prime
);

  wire nand_1_out, nand_2_out, not_1_out;

  not not_1 (not_1_out, D);
  nand nand_1 (nand_1_out, D, E);
  nand nand_2 (nand_2_out, E, not_1_out);
  nand nand_3 (Q, nand_1_out, Q_prime);
  nand nand_4 (Q_prime, Q, nand_2_out);
endmodule

module Gated_D_Latch_Active_High_With_NAND_Without_NOT (
  input  D,
  input  E,
  output Q,
  output Q_prime
);

  wire nand_1_out, nand_2_out;

  nand nand_1 (nand_1_out, D, E);
  nand nand_2 (nand_2_out, nand_1_out, E);
  nand nand_3 (Q, nand_1_out, Q_prime);
  nand nand_4 (Q_prime, Q, nand_2_out);
endmodule

module JK_Latch_Active_High_With_NOR (
  input  K,
  input  J,
  output Q,
  output Q_prime
);

  wire and_1_out, and_2_out;

  and and_1 (and_1_out, Q, K);
  and and_2 (and_2_out, J, Q_prime);
  nor nor_1 (Q, and_1_out, Q_prime);
  nor nor_2 (Q_prime, Q, and_2_out);
endmodule

module JK_Latch_Avtive_High_With_NAND (
  input  J,
  input  K,
  output Q,
  output Q_prime
);

  wire nand_1_out, nand_2_out;

  nand nand_1 (nand_1_out, Q_prime, J);
  nand nand_2 (nand_2_out, K, Q);
  nand nand_3 (Q, nand_1_out, Q_prime);
  nand nand_4 (Q_prime, Q, nand_2_out);
endmodule

module Gated_JK_Latch_Active_High (
  input  J,
  input  E,
  input  K,
  output Q,
  output Q_prime
);

  wire nand_1_out, nand_2_out;

  nand nand_1 (nand_1_out, Q_prime, J, E);
  nand nand_2 (nand_2_out, E, K, Q);
  nand nand_3 (Q, nand_1_out, Q_prime);
  nand nand_4 (Q_prime, Q, nand_2_out);
endmodule

module SR_Flip_Flop_Active_High_With_NAND (
  input  S,
  input  E,
  input  R,
  output Q,
  output Q_prime
);

  wire and_1_out, nand_1_out, nand_2_out, not_1_out;

  and and_1 (and_1_out, E, not_1_out);
  not not_1 (not_1_out, E);
  nand nand_1 (nand_1_out, S, and_1_out);
  nand nand_2 (nand_2_out, and_1_out, R);
  nand nand_3 (Q, nand_1_out, Q_prime);
  nand nand_4 (Q_prime, Q, nand_2_out);
endmodule

module D_Flip_Flop_Active_High (
  input  D,
  input  E,
  output Q,
  output Q_prime
);

  wire and_1_out, nand_1_out, nand_2_out, not_1_out;

  not not_1 (not_1_out, E);
  and and_1 (and_1_out, E, not_1_out);
  nand nand_1 (nand_1_out, D, and_1_out);
  nand nand_2 (nand_2_out, nand_1_out, and_1_out);
  nand nand_3 (Q, nand_1_out, Q_prime);
  nand nand_4 (Q_prime, Q, nand_2_out);
endmodule

module Master_Slave_D_Flip_Flop_Active_High (
  input  D,
  input  E,
  output Q,
  output Q_prime
);

  wire and_1_out, nand_1_out, nand_2_out, nand_3_out, nand_4_out, nand_5_out, nand_6_out, not_1_out,
       not_2_out;

  not not_1 (not_1_out, E);
  and and_1 (and_1_out, E, not_1_out);
  nand nand_1 (nand_1_out, D, and_1_out);
  nand nand_2 (nand_2_out, nand_1_out, and_1_out);
  not not_2 (not_2_out, and_1_out);
  nand nand_3 (nand_3_out, nand_1_out, nand_4_out);
  nand nand_4 (nand_4_out, nand_3_out, nand_2_out);
  nand nand_5 (nand_5_out, nand_3_out, not_2_out);
  nand nand_6 (nand_6_out, not_2_out, nand_4_out);
  nand nand_7 (Q, nand_5_out, Q_prime);
  nand nand_8 (Q_prime, Q, nand_6_out);
endmodule

module Master_Slave_D_Flip_Flop_Active_Low (
  input  D,
  input  E,
  output Q,
  output Q_prime
);

  wire and_1_out, and_2_out, and_3_out, nand_1_out, nand_2_out, nand_3_out, nand_4_out, not_1_out, not_2_out;

  not not_1 (not_1_out, E);
  and and_1 (and_1_out, E, not_1_out);
  nand nand_1 (nand_1_out, D, and_1_out);
  nand nand_2 (nand_2_out, nand_1_out, and_1_out);
  not not_2 (not_2_out, and_1_out);
  nand nand_3 (nand_3_out, nand_1_out, nand_4_out);
  nand nand_4 (nand_4_out, nand_3_out, nand_2_out);
  and and_2 (and_2_out, nand_3_out, not_2_out);
  and and_3 (and_3_out, not_2_out, nand_4_out);
  nor nor_1 (Q, and_2_out, Q_prime);
  nor nor_2 (Q_prime, Q, and_3_out);
endmodule

module JK_Flip_Flop_Active_High (
  input  J,
  input  E,
  input  K,
  output Q,
  output Q_prime
);

  wire and_1_out, nand_1_out, nand_2_out, not_1_out;

  and and_1 (and_1_out, E, not_1_out);
  not not_1 (not_1_out, E);
  nand nand_1 (nand_1_out, Q_prime, J, and_1_out);
  nand nand_2 (nand_2_out, and_1_out, K, Q);
  nand nand_3 (Q, nand_1_out, Q_prime);
  nand nand_4 (Q_prime, Q, nand_2_out);
endmodule

module JK_Flip_Flop_Active_High_With_Clear_And_Preset_Active_Low (
  input  Clear,
  input  J,
  input  E,
  input  K,
  input  Preset,
  output Q,
  output Q_prime
);

  wire and_1_out, nand_1_out, nand_2_out, not_1_out;

  and and_1 (and_1_out, E, not_1_out);
  not not_1 (not_1_out, E);
  nand nand_1 (nand_1_out, Q_prime, Clear, J, and_1_out);
  nand nand_2 (nand_2_out, and_1_out, K, Preset, Q);
  nand nand_3 (Q, nand_1_out, Preset, Q_prime);
  nand nand_4 (Q_prime, Q, Clear, nand_2_out);
endmodule

module T_Flip_Flop_Active_High (
  input  T,
  input  E,
  output Q,
  output Q_prime
);

  wire and_1_out, nand_1_out, nand_2_out, not_1_out;

  not not_1 (not_1_out, E);
  and and_1 (and_1_out, E, not_1_out);
  nand nand_1 (nand_1_out, Q_prime, T, and_1_out);
  nand nand_2 (nand_2_out, and_1_out, T, Q);
  nand nand_3 (Q, nand_1_out, Q_prime);
  nand nand_4 (Q_prime, Q, nand_2_out);
endmodule

module EX___OR_By_NAND (
  input  in_1,
  input  in_2,
  output out_3
);

  wire nand_1_out, nand_2_out, nand_3_out;

  nand nand_1 (nand_1_out, in_1, in_2);
  nand nand_2 (nand_2_out, in_1, nand_1_out);
  nand nand_3 (nand_3_out, nand_1_out, in_2);
  nand nand_4 (out_3, nand_2_out, nand_3_out);
endmodule

module EX___NOR_By_NOR (
  input  in_1,
  input  in_2,
  output out_3
);

  wire nor_1_out, nor_2_out, nor_3_out;

  nor nor_1 (nor_1_out, in_1, in_2);
  nor nor_2 (nor_2_out, in_1, nor_1_out);
  nor nor_3 (nor_3_out, nor_1_out, in_2);
  nor nor_4 (out_3, nor_2_out, nor_3_out);
endmodule

module A____B___C___D__By_NAND (
  input  C,
  input  A,
  input  B,
  input  D,
  output X
);

  wire nand_1_out, nand_2_out, nand_3_out;

  nand nand_1 (nand_1_out, A, B);
  nand nand_2 (nand_2_out, C, nand_1_out);
  nand nand_3 (nand_3_out, nand_1_out, D);
  nand nand_4 (X, nand_2_out, nand_3_out);
endmodule

module A_B____CD_By_NOR (
  input  C,
  input  A,
  input  B,
  input  D,
  output X
);

  wire nor_1_out, nor_2_out, nor_3_out;

  nor nor_1 (nor_1_out, A, B);
  nor nor_2 (nor_2_out, C, nor_1_out);
  nor nor_3 (nor_3_out, nor_1_out, D);
  nor nor_4 (X, nor_2_out, nor_3_out);
endmodule

module IC_74293 (
  input  VCC,
  input  R01,
  input  R02,
  output QA,
  output QB,
  output QC,
  output QD
);

  wire Clock_A_out, Clock_B_out, nand_1_out, not_1_out, not_2_out, not_3_out, not_4_out, not_5_out, not_6_out;

  Clock Clock_A (.out(Clock_A_out));
  Clock Clock_B (.out(Clock_B_out));
  not not_1 (not_1_out, Clock_A_out);
  not not_2 (not_2_out, VCC);
  nand nand_1 (nand_1_out, R01, R02);
  J_K_Flip_Flop j_k_ff_1 (
    .J(VCC), .clk(not_1_out), .K(VCC), .Q(QA), .preset(not_2_out), .reset(not_3_out));  // open: Qn, en
  not not_3 (not_3_out, nand_1_out);
  not not_4 (not_4_out, Clock_B_out);
  J_K_Flip_Flop j_k_ff_2 (
    .J(VCC), .clk(not_4_out), .K(VCC), .Q(QB), .preset(not_2_out), .reset(not_3_out));  // open: Qn, en
  J_K_Flip_Flop j_k_ff_3 (
    .J(VCC), .clk(not_5_out), .K(VCC), .Q(QC), .preset(not_2_out), .reset(not_3_out));  // open: Qn, en
  not not_5 (not_5_out, QB);
  not not_6 (not_6_out, QC);
  J_K_Flip_Flop j_k_ff_4 (
    .J(VCC), .clk(not_6_out), .K(VCC), .Q(QD), .preset(not_2_out), .reset(not_3_out));  // open: Qn, en
endmodule

module Ring_Counter (
  input  in_1,
  output out_2,
  output out_3,
  output out_4,
  output out_5
);

  wire clock_1_out;

  Clock clock_1 (.out(clock_1_out));
  D_Flip_Flop #(.trigger("high")) d_ff_1 (
    .clk(clock_1_out), .D(out_5), .Q(out_2), .preset(in_1));  // open: Qn, en, reset
  D_Flip_Flop #(.trigger("high")) d_ff_2 (
    .clk(clock_1_out), .D(out_2), .Q(out_3), .reset(in_1));  // open: Qn, preset, en
  D_Flip_Flop #(.trigger("high")) d_ff_3 (
    .clk(clock_1_out), .D(out_3), .Q(out_4), .reset(in_1));  // open: Qn, preset, en
  D_Flip_Flop #(.trigger("high")) d_ff_4 (
    .clk(clock_1_out), .D(out_4), .Q(out_5), .reset(in_1));  // open: Qn, preset, en
endmodule

module test (
  input  Input_1,
  input  Input_2,
  output Output
);

  // _7400 7400_1: pin names not known; wires that end beside it: Input_1, Input_2, Output, 1'b0, 1'b1
endmodule

module test1 (
  input  A,
  input  B,
  input  C,
  input  A_2,
  input  B_2,
  input  C_2,
  output X,
  output Y
);

  wire and_1_out, not_1_out, not_2_out, or_2_out;

  and and_1 (and_1_out, A, B);
  not not_1 (not_1_out, C);
  not not_2 (not_2_out, C_2);
  or or_1 (X, and_1_out, not_1_out);
  or or_2 (or_2_out, A_2, B_2);
  and and_2 (Y, or_2_out, not_2_out);
endmodule

module test2 (
  input  A,
  input  B,
  input  C,
  input  A_2,
  input  B_2,
  input  C_2,
  output Y,
  output X
);

  wire n7404_1_p3, n7404_2_p3, n7408_1_p3, n7432_2_p3;

  // _7408 7408_1: pin names not known; wires that end beside it: A_2, B_2, n7408_1_p3, 1'b1
  // _7404 7404_1: pin names not known; wires that end beside it: 1'b0, C_2, n7404_1_p3, 1'b0, 1'b1
  // _7432 7432_1: pin names not known; wires that end beside it: n7408_1_p3, n7404_1_p3, X, 1'b0, 1'b1
  // _7432 7432_2: pin names not known; wires that end beside it: A, B, n7432_2_p3, 1'b1
  // _7404 7404_2: pin names not known; wires that end beside it: 1'b0, C, n7404_2_p3, 1'b0, 1'b1
  // _7408 7408_2: pin names not known; wires that end beside it: n7432_2_p3, n7404_2_p3, Y, 1'b0, 1'b1
endmodule

module test3 (
  input  M,
  input  N,
  input  P,
  input  A,
  input  B,
  output Z,
  output W
);

  wire not_1_out, not_2_out, not_3_out, or_1_out, or_2_out, or_3_out;

  or or_1 (or_1_out, M, N);
  not not_1 (not_1_out, M);
  not not_2 (not_2_out, N);
  not not_3 (not_3_out, P);
  or or_2 (or_2_out, not_1_out, P);
  or or_3 (or_3_out, not_2_out, not_3_out);
  and and_1 (Z, or_2_out, or_1_out, or_3_out);
  or or_4 (W, A, B);
endmodule

module test4 (
  input  M,
  input  N,
  input  P,
  output Z
);

  wire not_1_out, not_2_out, not_3_out, or_1_out, or_2_out, or_3_out;

  or or_1 (or_1_out, M, N);
  not not_1 (not_1_out, M);
  not not_2 (not_2_out, N);
  not not_3 (not_3_out, P);
  or or_2 (or_2_out, not_1_out, P);
  or or_3 (or_3_out, not_2_out, not_3_out);
  and and_1 (Z, or_2_out, or_1_out, or_3_out);
endmodule

module ga (
  input  M,
  input  N,
  input  P,
  input  A,
  input  B,
  output Z,
  output W
);

  wire n7408_1_p3, n7432_1_p3, n7432_1_p4, n7432_1_p6, n7432_1_p9, n7432_1_p10, n7432_1_p11;

  // _7432 7432_1: pin names not known; wires that end beside it: M, N, n7432_1_p3, n7432_1_p4, P, n7432_1_p6, 1'b0, 1'b1, n7432_1_p9, n7432_1_p10, n7432_1_p11, Z, 1'b0
  // _7432 7432_2: pin names not known; wires that end beside it: A, B, W, 1'b0, 1'b1
  // _7404 7404_1: pin names not known; wires that end beside it: M, n7432_1_p4, N, n7432_1_p9, P, n7432_1_p10, 1'b0, 1'b1
  // _7408 7408_1: pin names not known; wires that end beside it: n7432_1_p3, n7432_1_p6, n7408_1_p3, n7408_1_p3, n7432_1_p11, 1'b1
endmodule

module teste (
  output Output,
  output Output_2
);

  wire Input_2_2_out, Input_2_out;

  Clock Input_2 (.out(Input_2_out));
  // _7408 7408_1: pin names not known; wires that end beside it: 1'b1, Input_2_out, Output, 1'b0, 1'b1
  Clock Input_2_2 (.out(Input_2_2_out));
  // _7432 7432_1: pin names not known; wires that end beside it: 1'b1, Input_2_2_out, Output_2, 1'b0, 1'b1

  // Notes on the sheet:
  //   Input 1
  //   Input 1
endmodule

module gaga (
  output Output
);

  wire Input_out, not_1_out, not_2_out, not_3_out, not_4_out;

  Clock Input (.out(Input_out));
  not not_1 (not_1_out, Input_out);
  not not_2 (not_2_out, not_1_out);
  not not_3 (not_3_out, not_2_out);
  // NOT_Gate not_4 has open pins: in=open, out=not_4_out
  or or_1 (Output, Input_out, not_3_out);
  // AND_Gate and_1 has open pins: in1=not_4_out, out=open

  // Notes on the sheet:
  //   Delayed Input
endmodule

module cgag (
  output Output,
  output Output_2
);

  wire Input_2_out, Input_out, n7404_1_p2, n7404_1_p4, n7404_1_p6, n7404_2_p2, n7404_2_p4, n7404_2_p6;

  Clock Input (.out(Input_out));
  // _7404 7404_1: pin names not known; wires that end beside it: Input_out, n7404_1_p2, n7404_1_p2, n7404_1_p4, n7404_1_p4, n7404_1_p6, 1'b0, 1'b1, 1'b0
  // _7408 7408_1: pin names not known; wires that end beside it: Input_out, n7404_1_p6, Output, 1'b1
  Clock Input_2 (.out(Input_2_out));
  // _7404 7404_2: pin names not known; wires that end beside it: Input_2_out, n7404_2_p2, n7404_2_p2, n7404_2_p4, n7404_2_p4, n7404_2_p6, 1'b0, 1'b1, 1'b0
  // _7432 7432_1: pin names not known; wires that end beside it: Input_2_out, n7404_2_p6, Output_2, 1'b1
endmodule

module te (
  input  in_1,
  input  [3:0] B3B2B1B0,
  input  [3:0] A3A2A1A0,
  input  in_4,
  input  _1nocarry0carry,
  input  _1logic0arith,
  input  [3:0] S3S2S1S0,
  output out_8,
  output A_B,
  output [3:0] F3F2F1F0
);

  wire and_1_out, not_1_out;

  Clock clock_1 (.out(in_1));
  IC_74181 ic_74181_1 (
    .Cn(_1nocarry0carry), .M(_1logic0arith), .A0(A3A2A1A0[0]), .B0(B3B2B1B0[0]), .A1(A3A2A1A0[1]),
    .B1(B3B2B1B0[1]), .A2(A3A2A1A0[2]), .B2(B3B2B1B0[2]), .A3(A3A2A1A0[3]), .B3(B3B2B1B0[3]),
    .F0(F3F2F1F0[0]), .F1(F3F2F1F0[1]), .A_B(A_B), .F2(F3F2F1F0[2]), .F3(F3F2F1F0[3]), .S0(S3S2S1S0[0]),
    .S1(S3S2S1S0[1]), .S2(S3S2S1S0[2]), .S3(S3S2S1S0[3]));  // open: P, Cn_4, G
  not not_1 (not_1_out, in_1);
  and and_1 (and_1_out, in_1, not_1_out);
  D_Flip_Flop #(.trigger("high")) d_ff_1 (.clk(and_1_out), .D(in_4), .Q(out_8));  // open: Qn, preset, en, reset
endmodule

module IC_74181 (
  input  Cn,
  input  M,
  input  A0,
  input  B0,
  input  A1,
  input  B1,
  input  A2,
  input  B2,
  input  A3,
  input  B3,
  input  S0,
  input  S1,
  input  S2,
  input  S3,
  output F0,
  output F1,
  output F2,
  output A_B,
  output F3,
  output P,
  output Cn_4,
  output G
);

  wire and_1_out, and_2_out, and_3_out, and_4_out, and_5_out, and_6_out, and_7_out, and_9_out, and_10_out,
       and_11_out, and_12_out, and_13_out, and_14_out, and_15_out, and_16_out, and_17_out, and_18_out,
       and_19_out, and_20_out, and_21_out, and_22_out, and_23_out, and_24_out, and_25_out, and_26_out,
       and_27_out, and_28_out, and_29_out, and_30_out, and_31_out, and_32_out, and_33_out, and_34_out,
       nand_1_out, nand_3_out, nor_1_out, nor_2_out, nor_3_out, nor_4_out, nor_5_out, nor_6_out, nor_7_out,
       nor_8_out, nor_9_out, nor_10_out, nor_11_out, not_1_out, not_2_out, not_3_out, not_4_out, not_5_out,
       xor_2_out, xor_4_out, xor_6_out, xor_8_out;

  nand nand_1 (nand_1_out, Cn, not_1_out);
  not not_1 (not_1_out, M);
  xor xor_1 (F0, nand_1_out, xor_2_out);
  and and_1 (and_1_out, A0, A0);
  xor xor_2 (xor_2_out, nor_1_out, nor_3_out);
  and and_2 (and_2_out, B0, S0);
  and and_3 (and_3_out, S1, not_2_out);
  nor nor_1 (nor_1_out, and_1_out, and_2_out, and_3_out);
  and and_4 (and_4_out, not_1_out, nor_1_out);
  not not_2 (not_2_out, B0);
  and and_5 (and_5_out, not_2_out, S2, A0);
  and and_6 (and_6_out, not_1_out, nor_3_out, Cn);
  nor nor_2 (nor_2_out, and_4_out, and_6_out);
  xor xor_3 (F1, nor_2_out, xor_4_out);
  and and_7 (and_7_out, A0, S3, B0);
  nor nor_3 (nor_3_out, and_5_out, and_7_out);
  xor xor_4 (xor_4_out, nor_4_out, nor_6_out);
  and and_8 (A_B, F0, F1, F2, F3);
  and and_9 (and_9_out, A1, A1);
  and and_10 (and_10_out, B1, S0);
  nor nor_4 (nor_4_out, and_9_out, and_10_out, and_12_out);
  and and_11 (and_11_out, not_1_out, nor_4_out);
  and and_12 (and_12_out, S1, not_3_out);
  and and_13 (and_13_out, not_1_out, nor_1_out, nor_6_out);
  and and_14 (and_14_out, not_1_out, Cn, nor_3_out, nor_6_out);
  nor nor_5 (nor_5_out, and_11_out, and_13_out, and_14_out);
  xor xor_5 (F2, nor_5_out, xor_6_out);
  not not_3 (not_3_out, B1);
  and and_15 (and_15_out, not_3_out, S2, A1);
  xor xor_6 (xor_6_out, nor_8_out, nor_9_out);
  and and_16 (and_16_out, A1, S3, B1);
  nor nor_6 (nor_6_out, and_15_out, and_16_out);
  and and_17 (and_17_out, not_1_out, nor_8_out);
  and and_18 (and_18_out, not_1_out, nor_4_out, nor_9_out);
  nor nor_7 (nor_7_out, and_17_out, and_18_out, and_21_out, and_23_out);
  and and_19 (and_19_out, B2, S0);
  and and_20 (and_20_out, A2, A2);
  nor nor_8 (nor_8_out, and_20_out, and_19_out, and_22_out);
  and and_21 (and_21_out, not_1_out, nor_1_out, nor_6_out, nor_9_out);
  xor xor_7 (F3, nor_7_out, xor_8_out);
  and and_22 (and_22_out, S1, not_4_out);
  and and_23 (and_23_out, not_1_out, Cn, nor_3_out, nor_6_out, nor_9_out);
  not not_4 (not_4_out, B2);
  and and_24 (and_24_out, not_4_out, S2, A2);
  nor nor_9 (nor_9_out, and_24_out, and_25_out);
  xor xor_8 (xor_8_out, nor_10_out, nor_11_out);
  and and_25 (and_25_out, A2, S3, B2);
  and and_26 (and_26_out, A3, A3);
  nand nand_2 (P, nor_3_out, nor_6_out, nor_9_out, nor_11_out);
  and and_27 (and_27_out, B3, S0);
  nor nor_10 (nor_10_out, and_26_out, and_27_out, and_28_out);
  nand nand_3 (nand_3_out, Cn, nor_3_out, nor_6_out, nor_9_out, nor_11_out);
  nand nand_4 (Cn_4, nand_3_out, G);
  not not_5 (not_5_out, B3);
  and and_28 (and_28_out, S1, not_5_out);
  and and_29 (and_29_out, nor_1_out, nor_6_out, nor_9_out, nor_11_out);
  and and_30 (and_30_out, not_5_out, S2, A3);
  nor nor_11 (nor_11_out, and_30_out, and_32_out);
  and and_31 (and_31_out, nor_4_out, nor_9_out, nor_11_out);
  nor nor_12 (G, and_29_out, and_31_out, and_33_out, and_34_out);
  and and_32 (and_32_out, A3, S3, B3);
  and and_33 (and_33_out, nor_8_out, nor_11_out);
  and and_34 (and_34_out, nor_10_out, nor_10_out);
endmodule

module as (
  input  A0,
  input  B0,
  input  A1,
  input  B1,
  input  A2,
  input  B2,
  input  A3,
  input  B3,
  output P
);

  wire and_1_out, and_2_out, and_3_out, and_4_out;

  and and_1 (and_1_out, A3, B3);
  and and_2 (and_2_out, A2, B2);
  and and_3 (and_3_out, A1, B1);
  and and_4 (and_4_out, A0, B0);
  or or_1 (P, and_1_out, and_2_out, and_3_out, and_4_out);
endmodule

module Egde_Detector_LOW_To_HIGH_Active_High (
  input  INPUT,
  output OUTPUT
);

  wire not_1_out;

  not not_1 (not_1_out, INPUT);
  and and_1 (OUTPUT, INPUT, not_1_out);

  // Notes on the sheet:
  //   INPUT'
endmodule

module a (
  input  R,
  output Q,
  output Q_prime
);

  nor nor_1 (Q, R, Q_prime);
  nor nor_2 (Q_prime, Q, R);
endmodule

module Asynchronous_Up_Counter_MOD_8_Using_JK (
  output A,
  output B,
  output C
);

  wire Clock_out;

  Clock Clock (.out(Clock_out));
  J_K_Flip_Flop #(.trigger("falling")) j_k_ff_1 (
    .J(1'b1), .clk(Clock_out), .K(1'b1), .Q(A));  // open: Qn, preset, en, reset
  J_K_Flip_Flop #(.trigger("falling")) j_k_ff_2 (.J(1'b1), .clk(A), .K(1'b1), .Q(B));  // open: Qn, preset, en, reset
  J_K_Flip_Flop #(.trigger("falling")) j_k_ff_3 (.J(1'b1), .clk(B), .K(1'b1), .Q(C));  // open: Qn, preset, en, reset
endmodule

module Asynchronous_Up_Counter_MOD_8_Using_D (
  output A,
  output B,
  output C
);

  wire Clock_out, d_ff_1_qn, d_ff_2_qn, d_ff_3_qn;

  Clock Clock (.out(Clock_out));
  D_Flip_Flop #(.trigger("falling")) d_ff_1 (
    .clk(Clock_out), .D(d_ff_1_qn), .Q(A), .Qn(d_ff_1_qn));  // open: preset, en, reset
  D_Flip_Flop #(.trigger("falling")) d_ff_2 (.clk(A), .D(d_ff_2_qn), .Q(B), .Qn(d_ff_2_qn));  // open: preset, en, reset
  D_Flip_Flop #(.trigger("falling")) d_ff_3 (.clk(B), .D(d_ff_3_qn), .Q(C), .Qn(d_ff_3_qn));  // open: preset, en, reset
endmodule

module Asynchronous_Down_Counter_MOD_8_Using_JK (
  output A,
  output B,
  output C
);

  wire Clock_out, j_k_ff_1_qn, j_k_ff_2_qn;

  Clock Clock (.out(Clock_out));
  J_K_Flip_Flop #(.trigger("falling")) j_k_ff_1 (
    .J(1'b1), .clk(Clock_out), .K(1'b1), .Q(A), .Qn(j_k_ff_1_qn));  // open: preset, en, reset
  J_K_Flip_Flop #(.trigger("falling")) j_k_ff_2 (
    .J(1'b1), .clk(j_k_ff_1_qn), .K(1'b1), .Q(B), .Qn(j_k_ff_2_qn));  // open: preset, en, reset
  J_K_Flip_Flop #(.trigger("falling")) j_k_ff_3 (
    .J(1'b1), .clk(j_k_ff_2_qn), .K(1'b1), .Q(C));  // open: Qn, preset, en, reset
endmodule

module Asynchronous_Down_Counter_MOD_8_Using_D (
  output A,
  output B,
  output C
);

  wire Clock_out, d_ff_1_qn, d_ff_2_qn, d_ff_3_qn;

  Clock Clock (.out(Clock_out));
  D_Flip_Flop #(.trigger("falling")) d_ff_1 (
    .clk(Clock_out), .D(d_ff_1_qn), .Q(A), .Qn(d_ff_1_qn));  // open: preset, en, reset
  D_Flip_Flop #(.trigger("falling")) d_ff_2 (
    .clk(d_ff_1_qn), .D(d_ff_2_qn), .Q(B), .Qn(d_ff_2_qn));  // open: preset, en, reset
  D_Flip_Flop #(.trigger("falling")) d_ff_3 (
    .clk(d_ff_2_qn), .D(d_ff_3_qn), .Q(C), .Qn(d_ff_3_qn));  // open: preset, en, reset
endmodule

module Asynchronous_Up_Counter_MOD_10_Using_JK (
  output A,
  output B,
  output C,
  output D
);

  wire and_1_out, Clock_out;

  Clock Clock (.out(Clock_out));
  J_K_Flip_Flop #(.trigger("falling")) j_k_ff_1 (
    .J(1'b1), .clk(Clock_out), .K(1'b1), .Q(A), .reset(and_1_out));  // open: Qn, preset, en
  J_K_Flip_Flop #(.trigger("falling")) j_k_ff_2 (
    .J(1'b1), .clk(A), .K(1'b1), .Q(B), .reset(and_1_out));  // open: Qn, preset, en
  J_K_Flip_Flop #(.trigger("falling")) j_k_ff_3 (
    .J(1'b1), .clk(B), .K(1'b1), .Q(C), .reset(and_1_out));  // open: Qn, preset, en
  J_K_Flip_Flop #(.trigger("falling")) j_k_ff_4 (
    .J(1'b1), .clk(C), .K(1'b1), .Q(D), .reset(and_1_out));  // open: Qn, preset, en
  and and_1 (and_1_out, B, D);
endmodule

module Asynchronous_Up_Counter_MOD_10_Using_D (
  output A,
  output B,
  output C,
  output D
);

  wire and_1_out, Clock_out, d_ff_1_qn, d_ff_2_qn, d_ff_3_qn, d_ff_4_qn;

  Clock Clock (.out(Clock_out));
  D_Flip_Flop #(.trigger("falling")) d_ff_1 (
    .clk(Clock_out), .D(d_ff_1_qn), .Q(A), .Qn(d_ff_1_qn), .reset(and_1_out));  // open: preset, en
  D_Flip_Flop #(.trigger("falling")) d_ff_2 (
    .clk(A), .D(d_ff_2_qn), .Q(B), .Qn(d_ff_2_qn), .reset(and_1_out));  // open: preset, en
  D_Flip_Flop #(.trigger("falling")) d_ff_3 (
    .clk(B), .D(d_ff_3_qn), .Q(C), .Qn(d_ff_3_qn), .reset(and_1_out));  // open: preset, en
  D_Flip_Flop #(.trigger("falling")) d_ff_4 (
    .clk(C), .D(d_ff_4_qn), .Q(D), .Qn(d_ff_4_qn), .reset(and_1_out));  // open: preset, en
  and and_1 (and_1_out, B, D);
endmodule

module Asynchronous_Up_Counter_4_To_12_Using_JK (
  output A,
  output B,
  output C,
  output D
);

  wire and_1_out, Clock_out;

  Clock Clock (.out(Clock_out));
  J_K_Flip_Flop #(.trigger("falling")) j_k_ff_1 (
    .J(1'b1), .clk(Clock_out), .K(1'b1), .Q(A), .reset(and_1_out));  // open: Qn, preset, en
  J_K_Flip_Flop #(.trigger("falling")) j_k_ff_2 (
    .J(1'b1), .clk(A), .K(1'b1), .Q(B), .reset(and_1_out));  // open: Qn, preset, en
  J_K_Flip_Flop #(.trigger("falling")) j_k_ff_3 (
    .J(1'b1), .clk(B), .K(1'b1), .Q(C), .preset(and_1_out));  // open: Qn, en, reset
  J_K_Flip_Flop #(.trigger("falling")) j_k_ff_4 (
    .J(1'b1), .clk(C), .K(1'b1), .Q(D), .reset(and_1_out));  // open: Qn, preset, en
  and and_1 (and_1_out, A, C, D);
endmodule

module Asynchronous_Up_Counter_4_To_12_Uisng_D (
  output A,
  output B,
  output C,
  output D
);

  wire and_1_out, Clock_out, d_ff_1_qn, d_ff_2_qn, d_ff_3_qn, d_ff_4_qn;

  Clock Clock (.out(Clock_out));
  D_Flip_Flop #(.trigger("falling")) d_ff_1 (
    .clk(Clock_out), .D(d_ff_1_qn), .Q(A), .Qn(d_ff_1_qn), .reset(and_1_out));  // open: preset, en
  D_Flip_Flop #(.trigger("falling")) d_ff_2 (
    .clk(A), .D(d_ff_2_qn), .Q(B), .Qn(d_ff_2_qn), .reset(and_1_out));  // open: preset, en
  D_Flip_Flop #(.trigger("falling")) d_ff_3 (
    .clk(B), .D(d_ff_3_qn), .Q(C), .Qn(d_ff_3_qn), .preset(and_1_out));  // open: en, reset
  D_Flip_Flop #(.trigger("falling")) d_ff_4 (
    .clk(C), .D(d_ff_4_qn), .Q(D), .Qn(d_ff_4_qn), .reset(and_1_out));  // open: preset, en
  and and_1 (and_1_out, A, C, D);
endmodule

module Asynchronous_Down_Counter_12_To_4_Using_JK (
  output A,
  output B,
  output C,
  output D
);

  wire and_1_out, Clock_out, j_k_ff_1_qn, j_k_ff_2_qn, j_k_ff_3_qn, j_k_ff_4_qn;

  Clock Clock (.out(Clock_out));
  J_K_Flip_Flop #(.trigger("falling")) j_k_ff_1 (
    .J(1'b1), .clk(Clock_out), .K(1'b1), .Q(A), .Qn(j_k_ff_1_qn), .reset(and_1_out));  // open: preset, en
  J_K_Flip_Flop #(.trigger("falling")) j_k_ff_2 (
    .J(1'b1), .clk(j_k_ff_1_qn), .K(1'b1), .Q(B), .Qn(j_k_ff_2_qn), .reset(and_1_out));  // open: preset, en
  J_K_Flip_Flop #(.trigger("falling")) j_k_ff_3 (
    .J(1'b1), .clk(j_k_ff_2_qn), .K(1'b1), .Q(C), .Qn(j_k_ff_3_qn), .preset(and_1_out));  // open: en, reset
  J_K_Flip_Flop #(.trigger("falling")) j_k_ff_4 (
    .J(1'b1), .clk(j_k_ff_3_qn), .K(1'b1), .Q(D), .Qn(j_k_ff_4_qn), .preset(and_1_out));  // open: en, reset
  and and_1 (and_1_out, j_k_ff_3_qn, j_k_ff_4_qn);
endmodule

module Asynchronous_Down_Counter_12_To_4_Using_D (
  output A,
  output B,
  output C,
  output D
);

  wire and_1_out, Clock_out, d_ff_1_qn, d_ff_2_qn, d_ff_3_qn, d_ff_4_qn;

  Clock Clock (.out(Clock_out));
  D_Flip_Flop #(.trigger("falling")) d_ff_1 (
    .clk(Clock_out), .D(d_ff_1_qn), .Q(A), .Qn(d_ff_1_qn), .reset(and_1_out));  // open: preset, en
  D_Flip_Flop #(.trigger("falling")) d_ff_2 (
    .clk(d_ff_1_qn), .D(d_ff_2_qn), .Q(B), .Qn(d_ff_2_qn), .reset(and_1_out));  // open: preset, en
  D_Flip_Flop #(.trigger("falling")) d_ff_3 (
    .clk(d_ff_2_qn), .D(d_ff_3_qn), .Q(C), .Qn(d_ff_3_qn), .preset(and_1_out));  // open: en, reset
  D_Flip_Flop #(.trigger("falling")) d_ff_4 (
    .clk(d_ff_3_qn), .D(d_ff_4_qn), .Q(D), .Qn(d_ff_4_qn), .preset(and_1_out));  // open: en, reset
  and and_1 (and_1_out, d_ff_3_qn, d_ff_4_qn);
endmodule

module Synchronous_Up_Counter_MOD_16_Using_JK (
  output A,
  output B,
  output C,
  output D
);

  wire and_1_out, and_2_out, Clock_out;

  Clock Clock (.out(Clock_out));
  J_K_Flip_Flop j_k_ff_1 (.J(1'b1), .clk(Clock_out), .K(1'b1), .Q(A));  // open: Qn, preset, en, reset
  J_K_Flip_Flop j_k_ff_2 (.J(A), .clk(Clock_out), .K(A), .Q(B));  // open: Qn, preset, en, reset
  and and_1 (and_1_out, A, B);
  J_K_Flip_Flop j_k_ff_3 (.J(and_1_out), .clk(Clock_out), .K(and_1_out), .Q(C));  // open: Qn, preset, en, reset
  and and_2 (and_2_out, and_1_out, C);
  J_K_Flip_Flop j_k_ff_4 (.J(and_2_out), .clk(Clock_out), .K(and_2_out), .Q(D));  // open: Qn, preset, en, reset
endmodule

module Synchronous_Down_Counter_MOD_16_Using_JK (
  output A,
  output B,
  output C,
  output D
);

  wire and_1_out, and_2_out, Clock_out, j_k_ff_1_qn, j_k_ff_2_qn, j_k_ff_3_qn;

  Clock Clock (.out(Clock_out));
  J_K_Flip_Flop j_k_ff_1 (.J(1'b1), .clk(Clock_out), .K(1'b1), .Q(A), .Qn(j_k_ff_1_qn));  // open: preset, en, reset
  J_K_Flip_Flop j_k_ff_2 (
    .J(j_k_ff_1_qn), .clk(Clock_out), .K(j_k_ff_1_qn), .Q(B), .Qn(j_k_ff_2_qn));  // open: preset, en, reset
  and and_1 (and_1_out, j_k_ff_1_qn, j_k_ff_2_qn);
  J_K_Flip_Flop j_k_ff_3 (
    .J(and_1_out), .clk(Clock_out), .K(and_1_out), .Q(C), .Qn(j_k_ff_3_qn));  // open: preset, en, reset
  and and_2 (and_2_out, and_1_out, j_k_ff_3_qn);
  J_K_Flip_Flop j_k_ff_4 (.J(and_2_out), .clk(Clock_out), .K(and_2_out), .Q(D));  // open: Qn, preset, en, reset
endmodule

module datt (
  input  [3:0] in_1,
  input  in_2,
  input  in_3,
  input  in_4,
  input  [2:0] in_5,
  input  [2:0] in_6,
  output out_7,
  output [3:0] out_8,
  output [7:0] out_9
);

  wire clock_1_out;

  Clock clock_1 (.out(clock_1_out));
  // _74138 74138_1: pin names not known; wires that end beside it: in_5[0], in_5[1], in_5[2], in_6[0], in_6[1], in_6[2], out_9[7], 1'b0, 1'b1, out_9[0], out_9[1], out_9[2], out_9[3], out_9[4], out_9[5], out_9[6]
  // _74161 74161_1: pin names not known; wires that end beside it: clock_1_out, in_1[0], in_1[1], in_1[2], in_1[3], in_4, 1'b0, 1'b1, out_7, out_8[0], out_8[1], out_8[2], out_8[3], in_3, in_2
endmodule

module LAB_3_Simulation (
  input  D,
  input  D_2,
  input  x,
  input  CLR_prime,
  input  PRE_prime,
  output Q_prime,
  output Q,
  output QA,
  output QB,
  output QC,
  output QA_2,
  output QB_2,
  output QC_2,
  output Q_2,
  output Q_prime_2,
  output z
);

  wire and_1_out, Clock_2_out, CLOCK_3_out, Clock_4_out, Clock_5_out, Clock_out, d_ff_1_q, d_ff_1_qn,
       d_ff_2_q, d_ff_3_q, j_k_ff_2_q, j_k_ff_2_qn, n7404_1_p2, n7474_1__5__q1, n7474_1__9__q2, not_1_out,
       not_2_out, not_3_out;

  Clock Clock (.out(Clock_out));
  Clock Clock_2 (.out(Clock_2_out));
  // _7404 7404_1: pin names not known; wires that end beside it: D, n7404_1_p2, 1'b0, 1'b1
  not not_1 (not_1_out, D_2);
  _7473 u_7473_1 (
    .CLK1__1(Clock_out), .CLR1__2(1'b1), .K1__3(n7404_1_p2), .VCC__4(1'b1), ._14__J1(D),
    ._13__Q1_prime(Q_prime), ._12__Q1(Q), ._11__GND(1'b0));  // open: CLK2__5, CLR2__6, J2__7, _10__K2, _9__Q2, _8__Q2_prime
  J_K_Flip_Flop j_k_ff_1 (
    .J(D_2), .clk(Clock_2_out), .K(not_1_out), .Q(Q_2), .Qn(Q_prime_2));  // open: preset, en, reset
  and and_1 (and_1_out, j_k_ff_2_q, x);
  Clock CLOCK_3 (.out(CLOCK_3_out));
  not not_2 (not_2_out, CLR_prime);
  not not_3 (not_3_out, PRE_prime);
  D_Flip_Flop #(.trigger("falling")) d_ff_1 (
    .clk(CLOCK_3_out), .D(and_1_out), .Q(d_ff_1_q), .Qn(d_ff_1_qn), .preset(not_3_out), .reset(not_2_out));  // open: en
  Clock Clock_4 (.out(Clock_4_out));
  Clock Clock_5 (.out(Clock_5_out));
  J_K_Flip_Flop #(.trigger("falling")) j_k_ff_2 (
    .J(d_ff_1_qn), .clk(CLOCK_3_out), .K(d_ff_1_q), .Q(j_k_ff_2_q), .Qn(j_k_ff_2_qn), .preset(not_3_out),
    .reset(not_2_out));  // open: en
  _7474 u_7474_1 (
    ._1__CLR1(1'b1), ._2__D1(QA), ._3__CLK1(Clock_4_out), ._4__PR1(1'b1), ._5__Q1(n7474_1__5__q1),
    ._6__nQ1(QA), ._7__GND(1'b0), ._14__Vcc(1'b1), ._13__CLR2(1'b1), ._12__D2(QB),
    ._11__CLK2(n7474_1__5__q1), ._10__PR2(1'b1), ._9__Q2(n7474_1__9__q2), ._8__nQ2(QB));
  D_Flip_Flop d_ff_2 (.clk(Clock_5_out), .D(QA_2), .Q(d_ff_2_q), .Qn(QA_2));  // open: preset, en, reset
  or or_1 (z, d_ff_1_qn, j_k_ff_2_qn);
  D_Flip_Flop d_ff_3 (.clk(d_ff_2_q), .D(QB_2), .Q(d_ff_3_q), .Qn(QB_2));  // open: preset, en, reset
  _7474 u_7474_2 (
    ._1__CLR1(1'b1), ._2__D1(QC), ._3__CLK1(n7474_1__9__q2), ._4__PR1(1'b1), ._6__nQ1(QC), ._7__GND(1'b0),
    ._14__Vcc(1'b1));  // open: _5__Q1, _13__CLR2, _12__D2, _11__CLK2, _10__PR2, _9__Q2, _8__nQ2
  D_Flip_Flop d_ff_4 (.clk(d_ff_3_q), .D(QC_2), .Qn(QC_2));  // open: Q, preset, en, reset
endmodule

module _7473 (
  input  CLK1__1,
  input  _14__J1,
  input  CLR1__2,
  input  K1__3,
  input  VCC__4,
  input  _11__GND,
  input  CLK2__5,
  input  _10__K2,
  input  CLR2__6,
  input  J2__7,
  output _13__Q1_prime,
  output _12__Q1,
  output _9__Q2,
  output _8__Q2_prime
);

  wire not_1_out, not_2_out;

  not not_1 (not_1_out, CLR1__2);
  not not_2 (not_2_out, CLR2__6);
  J_K_Flip_Flop #(.trigger("falling")) j_k_ff_1 (
    .J(_14__J1), .clk(CLK1__1), .K(K1__3), .Q(_12__Q1), .Qn(_13__Q1_prime), .reset(not_1_out));  // open: preset, en
  J_K_Flip_Flop #(.trigger("falling")) j_k_ff_2 (
    .J(J2__7), .clk(CLK2__5), .K(_10__K2), .Q(_9__Q2), .Qn(_8__Q2_prime), .reset(not_2_out));  // open: preset, en
endmodule

module _7474 (
  input  _1__CLR1,
  input  _14__Vcc,
  input  _2__D1,
  input  _13__CLR2,
  input  _3__CLK1,
  input  _12__D2,
  input  _4__PR1,
  input  _11__CLK2,
  input  _10__PR2,
  input  _7__GND,
  output _5__Q1,
  output _6__nQ1,
  output _9__Q2,
  output _8__nQ2
);

  wire not_1_out, not_2_out, not_3_out, not_4_out;

  not not_1 (not_1_out, _1__CLR1);
  D_Flip_Flop d_ff_1 (
    .clk(_3__CLK1), .D(_2__D1), .Q(_5__Q1), .Qn(_6__nQ1), .preset(not_2_out), .reset(not_1_out));  // open: en
  not not_2 (not_2_out, _4__PR1);
  not not_3 (not_3_out, _13__CLR2);
  D_Flip_Flop d_ff_2 (
    .clk(_11__CLK2), .D(_12__D2), .Q(_9__Q2), .Qn(_8__nQ2), .preset(not_4_out), .reset(not_3_out));  // open: en
  not not_4 (not_4_out, _10__PR2);
endmodule

module LAB_4_Simulation (
  input  B0,
  input  B1,
  input  B2,
  input  B3,
  input  A0,
  input  A1,
  input  A2,
  input  A3,
  input  in_9,
  input  A3_2,
  input  A2_2,
  input  A1_2,
  input  A0_2,
  input  B3_2,
  input  B2_2,
  input  B1_2,
  input  B0_2,
  output A,
  output B,
  output C,
  output D,
  output COUT,
  output S0,
  output S1,
  output S2,
  output S3,
  output A_2,
  output B_2,
  output C_2,
  output D_2,
  output COUT_2,
  output S3_2,
  output S2_2,
  output S1_2,
  output S0_2
);

  wire Clock_2_out, Clock_out, full_adder_1_cout, full_adder_2_cout, full_adder_3_cout, n7400_1_p3,
       nand_1_out, nand_2_out, not_1_out, undriven, undriven_2;

  nand nand_1 (nand_1_out, undriven, undriven_2);
  Full_Adder full_adder_1 (.A(A0), .B(B0), .CIN(in_9), .SUM(S0), .COUT(full_adder_1_cout));
  Full_Adder full_adder_2 (.A(A1), .B(B1), .CIN(full_adder_1_cout), .SUM(S1), .COUT(full_adder_2_cout));
  _7483 u_7483_1 (
    ._1__A4(A3_2), ._2__S3(S2_2), ._3__A3(A2_2), ._4__B3(B2_2), ._5__Vcc(1'b1), ._6__S2(S1_2), ._7__B2(B1_2),
    ._8__A2(A1_2), ._16__B4(B3_2), ._15__S4(S3_2), ._14__Cout(COUT_2), ._13__Cin(1'b0), ._12__GND(1'b0),
    ._11__B1(B0_2), ._10__A1(A0_2), ._9__S1(S0_2));
  Full_Adder full_adder_3 (.A(A2), .B(B2), .CIN(full_adder_2_cout), .SUM(S2), .COUT(full_adder_3_cout));
  Full_Adder full_adder_4 (.A(A3), .B(B3), .CIN(full_adder_3_cout), .SUM(S3), .COUT(COUT));
  Clock Clock (.out(Clock_out));
  J_K_Flip_Flop #(.trigger("falling")) j_k_ff_1 (
    .J(1'b1), .clk(Clock_out), .K(1'b1), .Q(A), .reset(not_1_out));  // open: Qn, preset, en
  J_K_Flip_Flop #(.trigger("falling")) j_k_ff_2 (
    .J(1'b1), .clk(A), .K(1'b1), .Q(B), .reset(not_1_out));  // open: Qn, preset, en
  Clock Clock_2 (.out(Clock_2_out));
  J_K_Flip_Flop #(.trigger("falling")) j_k_ff_3 (
    .J(1'b1), .clk(B), .K(1'b1), .Q(C), .reset(not_1_out));  // open: Qn, preset, en
  J_K_Flip_Flop #(.trigger("falling")) j_k_ff_4 (
    .J(1'b1), .clk(C), .K(1'b1), .Q(D), .reset(not_1_out));  // open: Qn, preset, en
  _7473 u_7473_1 (
    .CLK1__1(Clock_2_out), .CLR1__2(n7400_1_p3), .K1__3(1'b1), .VCC__4(1'b1), .CLK2__5(A_2),
    .CLR2__6(n7400_1_p3), .J2__7(1'b1), ._14__J1(1'b1), ._12__Q1(A_2), ._11__GND(1'b0), ._10__K2(1'b1),
    ._9__Q2(B_2));  // open: _13__Q1_prime, _8__Q2_prime
  _7473 u_7473_2 (
    .CLK1__1(B_2), .CLR1__2(n7400_1_p3), .K1__3(1'b1), .VCC__4(1'b1), .CLK2__5(C_2), .CLR2__6(n7400_1_p3),
    .J2__7(1'b1), ._14__J1(1'b1), ._12__Q1(C_2), ._11__GND(1'b0), ._10__K2(1'b1), ._9__Q2(D_2));  // open: _13__Q1_prime, _8__Q2_prime
  nand nand_2 (nand_2_out, B, D);
  not not_1 (not_1_out, nand_2_out);
  // _7400 7400_1: pin names not known; wires that end beside it: B_2, D_2, n7400_1_p3, 1'b0, 1'b1

  // Notes on the sheet:
  //   QD (MSB)
  //   QB
  //   CLR'.
endmodule

// HA
module Half_Adder (
  input  A,
  input  B,
  output SUM,
  output CARRY
);

  xor xor_1 (SUM, A, B);
  and and_1 (CARRY, A, B);
endmodule

// FA
module Full_Adder (
  input  A,
  input  B,
  input  CIN,
  output SUM,
  output COUT
);

  wire half_adder_1_carry, half_adder_1_sum, half_adder_2_carry;

  Half_Adder half_adder_1 (.A(A), .B(B), .SUM(half_adder_1_sum), .CARRY(half_adder_1_carry));
  Half_Adder half_adder_2 (.A(half_adder_1_sum), .B(CIN), .SUM(SUM), .CARRY(half_adder_2_carry));
  or or_1 (COUT, half_adder_2_carry, half_adder_1_carry);
endmodule

module _7483 (
  input  _1__A4,
  input  _16__B4,
  input  _3__A3,
  input  _4__B3,
  input  _13__Cin,
  input  _5__Vcc,
  input  _12__GND,
  input  _11__B1,
  input  _7__B2,
  input  _10__A1,
  input  _8__A2,
  output _2__S3,
  output _15__S4,
  output _14__Cout,
  output _6__S2,
  output _9__S1
);

  wire and_1_out, and_2_out, and_3_out, and_4_out, and_5_out, and_6_out, and_7_out, and_8_out, and_9_out,
       and_10_out, and_11_out, and_12_out, and_13_out, and_14_out, nand_1_out, nand_2_out, nand_3_out,
       nand_4_out, nor_1_out, nor_2_out, nor_3_out, nor_4_out, nor_6_out, nor_7_out, nor_8_out, not_1_out,
       not_2_out, not_3_out, not_4_out, not_5_out, not_6_out;

  nand nand_1 (nand_1_out, _16__B4, _1__A4);
  nor nor_1 (nor_1_out, _16__B4, _1__A4);
  nand nand_2 (nand_2_out, _4__B3, _3__A3);
  nor nor_2 (nor_2_out, _4__B3, _3__A3);
  nand nand_3 (nand_3_out, _7__B2, _8__A2);
  nor nor_3 (nor_3_out, _7__B2, _8__A2);
  nand nand_4 (nand_4_out, _11__B1, _10__A1);
  nor nor_4 (nor_4_out, _11__B1, _10__A1);
  and and_1 (and_1_out, nor_2_out, nand_1_out);
  and and_2 (and_2_out, nor_3_out, nand_1_out, nand_2_out);
  and and_3 (and_3_out, nor_4_out, nand_1_out, nand_2_out, nand_3_out);
  and and_4 (and_4_out, nand_1_out, nand_2_out, nand_3_out, nand_4_out, not_2_out);
  not not_1 (not_1_out, nor_1_out);
  and and_5 (and_5_out, nor_3_out, nand_2_out);
  and and_6 (and_6_out, nor_4_out, nand_2_out, nand_3_out);
  and and_7 (and_7_out, nand_2_out, nand_3_out, nand_4_out, not_2_out);
  not not_2 (not_2_out, _13__Cin);
  not not_3 (not_3_out, nor_2_out);
  and and_8 (and_8_out, nor_4_out, nand_3_out);
  and and_9 (and_9_out, nand_3_out, nand_4_out, not_2_out);
  not not_4 (not_4_out, nor_3_out);
  and and_10 (and_10_out, nand_4_out, not_2_out);
  not not_5 (not_5_out, nor_4_out);
  not not_6 (not_6_out, not_2_out);
  nor nor_5 (_14__Cout, nor_1_out, and_1_out, and_2_out, and_3_out, and_4_out);
  and and_11 (and_11_out, nand_1_out, not_1_out);
  and and_12 (and_12_out, nand_2_out, not_3_out);
  and and_13 (and_13_out, nand_3_out, not_4_out);
  and and_14 (and_14_out, nand_4_out, not_5_out);
  xor xor_1 (_15__S4, and_11_out, nor_6_out);
  nor nor_6 (nor_6_out, nor_2_out, and_5_out, and_6_out, and_7_out);
  xor xor_2 (_2__S3, and_12_out, nor_7_out);
  nor nor_7 (nor_7_out, nor_3_out, and_8_out, and_9_out);
  xor xor_3 (_6__S2, and_13_out, nor_8_out);
  nor nor_8 (nor_8_out, nor_4_out, and_10_out);
  xor xor_4 (_9__S1, and_14_out, not_6_out);

  // Notes on the sheet:
  //   7483: 4-bit full adder
endmodule

module LAB_5_Simulation (
  input  [2:0] Input,
  input  [7:0] Data_Input,
  input  [2:0] Data_Selector,
  input  [7:0] A,
  input  [7:0] B,
  output [7:0] Output,
  output Q1,
  output Q0,
  output Q1_2,
  output Q0_2,
  output Output_2,
  output Q1_3,
  output Q0_3,
  output A_B,
  output A_B_2,
  output A_B_3,
  output Q1_4,
  output Q0_4,
  output Q1_5,
  output Q0_5
);

  wire Clock_2_out, Clock_3_out, Clock_4_out, Clock_5_out, Clock_out, D0_2_qn, D0_qn, n7404_1_p2,
       n7474_1__6__nq1, n7474_2__6__nq1, n7474_3__6__nq1, n7485_1_yeq, n7485_1_ygt, n7485_1_ylt, n7486_1_p3,
       n7486_2_p3, n74266_1__3__1y, xnor_1_out, xor_1_out;

  Clock Clock (.out(Clock_out));
  Clock Clock_2 (.out(Clock_2_out));
  Clock Clock_3 (.out(Clock_3_out));
  _7474 u_7474_1 (
    ._1__CLR1(1'b1), ._2__D1(n7474_1__6__nq1), ._3__CLK1(Clock_out), ._4__PR1(1'b1), ._5__Q1(Q0_3),
    ._6__nQ1(n7474_1__6__nq1), ._7__GND(1'b0), ._14__Vcc(1'b1), ._13__CLR2(1'b1), ._12__D2(n7404_1_p2),
    ._11__CLK2(Clock_out), ._10__PR2(1'b1), ._9__Q2(Q1_3));  // open: _8__nQ2
  D_Flip_Flop D1 (.clk(Clock_2_out), .D(xor_1_out), .Q(Q1_5));  // open: Qn, preset, en, reset
  xnor xnor_1 (xnor_1_out, Q1, Q0);
  D_Flip_Flop D1_2 (.clk(Clock_3_out), .D(xnor_1_out), .Q(Q1));  // open: Qn, preset, en, reset
  // _7486 7486_1: pin names not known; wires that end beside it: Q0_3, Q1_3, n7486_1_p3, 1'b0, 1'b1
  xor xor_1 (xor_1_out, Q1_5, D0_2_qn);
  D_Flip_Flop D0 (.clk(Clock_3_out), .D(D0_qn), .Q(Q0), .Qn(D0_qn));  // open: preset, en, reset
  // _7404 7404_1: pin names not known; wires that end beside it: n7486_1_p3, n7404_1_p2, 1'b0, 1'b1
  D_Flip_Flop D0_2 (.clk(Clock_2_out), .D(D0_2_qn), .Q(Q0_5), .Qn(D0_2_qn));  // open: preset, en, reset
  Clock Clock_4 (.out(Clock_4_out));
  Clock Clock_5 (.out(Clock_5_out));
  _7474 u_7474_2 (
    ._1__CLR1(1'b1), ._2__D1(n7474_2__6__nq1), ._3__CLK1(Clock_4_out), ._4__PR1(1'b1), ._5__Q1(Q0_4),
    ._6__nQ1(n7474_2__6__nq1), ._7__GND(1'b0), ._14__Vcc(1'b1), ._13__CLR2(1'b1), ._12__D2(n7486_2_p3),
    ._11__CLK2(Clock_4_out), ._10__PR2(1'b1), ._9__Q2(Q1_4));  // open: _8__nQ2
  _7474 u_7474_3 (
    ._1__CLR1(1'b1), ._2__D1(n7474_3__6__nq1), ._3__CLK1(Clock_5_out), ._4__PR1(1'b1), ._5__Q1(Q0_2),
    ._6__nQ1(n7474_3__6__nq1), ._7__GND(1'b0), ._14__Vcc(1'b1), ._13__CLR2(1'b1), ._12__D2(n74266_1__3__1y),
    ._11__CLK2(Clock_5_out), ._10__PR2(1'b1), ._9__Q2(Q1_2));  // open: _8__nQ2
  // _74151 74151_1: pin names not known; wires that end beside it: Data_Input[3], Data_Input[2], Data_Input[1], Data_Input[0], Output_2, 1'b0, 1'b0, 1'b1, Data_Input[4], Data_Input[5], Data_Input[6], Data_Input[7], Data_Selector[0], Data_Selector[1], Data_Selector[2]
  _74266 u_74266_1 (
    ._1__1A(Q0_2), ._2__1B(Q1_2), ._3__1Y(n74266_1__3__1y), ._7__GND(1'b0), ._14__Vcc(1'b1));  // open: _4__2Y, _5__2B, _6__2A, _13__4B, _12__4A, _11__4Y, _10__3Y, _9__3B, _8__3A
  // _7486 7486_2: pin names not known; wires that end beside it: n7474_2__6__nq1, Q1_4, n7486_2_p3, 1'b0, 1'b1
  // _74138 74138_1: pin names not known; wires that end beside it: Input[0], Input[1], Input[2], 1'b0, 1'b0, 1'b1, Output[7], 1'b0, 1'b1, Output[0], Output[1], Output[2], Output[3], Output[4], Output[5], Output[6]
  _7485 u_7485_1 (
    .B4(B[3]), .CLT(1'b0), .CEQ(1'b1), .CGT(1'b0), .YGT(n7485_1_ygt), .YEQ(n7485_1_yeq), .YLT(n7485_1_ylt),
    .GND(1'b0), .VCC(1'b1), .A4(A[3]), .B3(B[2]), .A3(A[2]), .A2(A[1]), .B2(B[1]), .A1(A[0]), .B1(B[0]));
  _7485 u_7485_2 (
    .B4(B[7]), .CLT(n7485_1_ylt), .CEQ(n7485_1_yeq), .CGT(n7485_1_ygt), .YGT(A_B_3), .YEQ(A_B_2), .YLT(A_B),
    .GND(1'b0), .VCC(1'b1), .A4(A[7]), .B3(B[6]), .A3(A[6]), .A2(A[5]), .B2(B[5]), .A1(A[4]), .B1(B[4]));
endmodule

module _74266 (
  input  _1__1A,
  input  _14__Vcc,
  input  _2__1B,
  input  _13__4B,
  input  _12__4A,
  input  _5__2B,
  input  _6__2A,
  input  _9__3B,
  input  _7__GND,
  input  _8__3A,
  output _3__1Y,
  output _4__2Y,
  output _11__4Y,
  output _10__3Y
);

  xnor xnor_1 (_3__1Y, _2__1B, _1__1A);
  xnor xnor_2 (_4__2Y, _5__2B, _6__2A);
  xnor xnor_3 (_11__4Y, _13__4B, _12__4A);
  xnor xnor_4 (_10__3Y, _8__3A, _9__3B);
endmodule

module _7485 (
  input  B4,
  input  CLT,
  input  VCC,
  input  A4,
  input  CEQ,
  input  B3,
  input  CGT,
  input  A3,
  input  A2,
  input  B2,
  input  A1,
  input  B1,
  input  GND,
  output YGT,
  output YEQ,
  output YLT
);

  wire and_1_out, and_2_out, and_3_out, and_4_out, and_5_out, and_6_out, and_7_out, and_8_out, and_9_out,
       and_10_out, and_11_out, and_12_out, and_13_out, and_14_out, and_16_out, and_17_out, and_18_out,
       and_19_out, and_20_out, and_21_out, nand_1_out, nand_2_out, nand_3_out, nand_4_out, nor_1_out,
       nor_2_out, nor_3_out, nor_4_out;

  nand nand_1 (nand_1_out, A4, B4);
  nand nand_2 (nand_2_out, A3, B3);
  nand nand_3 (nand_3_out, A2, B2);
  nand nand_4 (nand_4_out, A1, B1);
  and and_1 (and_1_out, A4, nand_1_out);
  and and_2 (and_2_out, nand_1_out, B4);
  and and_3 (and_3_out, A3, nand_2_out);
  and and_4 (and_4_out, nand_2_out, B3);
  and and_5 (and_5_out, A2, nand_3_out);
  and and_6 (and_6_out, nand_3_out, B2);
  and and_7 (and_7_out, A1, nand_4_out);
  and and_8 (and_8_out, nand_4_out, B1);
  nor nor_1 (nor_1_out, and_1_out, and_2_out);
  nor nor_2 (nor_2_out, and_3_out, and_4_out);
  nor nor_3 (nor_3_out, and_5_out, and_6_out);
  nor nor_4 (nor_4_out, and_7_out, and_8_out);
  and and_9 (and_9_out, B4, nand_1_out);
  and and_10 (and_10_out, B3, nand_2_out, nor_1_out);
  and and_11 (and_11_out, B2, nand_3_out, nor_1_out, nor_2_out);
  and and_12 (and_12_out, B1, nand_4_out, nor_1_out, nor_2_out, nor_3_out);
  and and_13 (and_13_out, nor_1_out, nor_2_out, nor_3_out, nor_4_out, CLT);
  and and_14 (and_14_out, nor_1_out, nor_2_out, nor_3_out, nor_4_out, CEQ);
  and and_15 (YEQ, nor_1_out, nor_2_out, CEQ, nor_3_out, nor_4_out);
  and and_16 (and_16_out, CEQ, nor_4_out, nor_3_out, nor_2_out, nor_1_out);
  and and_17 (and_17_out, CGT, nor_4_out, nor_3_out, nor_2_out, nor_1_out);
  and and_18 (and_18_out, nor_3_out, nor_2_out, nor_1_out, nand_4_out, A1);
  and and_19 (and_19_out, nor_2_out, nor_1_out, nand_3_out, A2);
  and and_20 (and_20_out, nor_1_out, nand_2_out, A3);
  and and_21 (and_21_out, nand_1_out, A4);
  nor nor_5 (YGT, and_9_out, and_10_out, and_11_out, and_12_out, and_13_out, and_14_out);
  nor nor_6 (YLT, and_16_out, and_17_out, and_18_out, and_19_out, and_20_out, and_21_out);
endmodule

module lab5recent (
  output Q1,
  output Q0,
  output Q1_2,
  output Q0_2
);

  wire Clock_2_out, Clock_out, D0_qn, n7474_1__6__nq1, n7486_1_p3, xor_1_out;

  Clock Clock (.out(Clock_out));
  D_Flip_Flop D1 (.clk(Clock_out), .D(xor_1_out), .Q(Q1_2));  // open: Qn, preset, en, reset
  xor xor_1 (xor_1_out, Q1_2, D0_qn);
  D_Flip_Flop D0 (.clk(Clock_out), .D(D0_qn), .Q(Q0_2), .Qn(D0_qn));  // open: preset, en, reset
  Clock Clock_2 (.out(Clock_2_out));
  _7474 u_7474_1 (
    ._1__CLR1(1'b1), ._2__D1(n7474_1__6__nq1), ._3__CLK1(Clock_2_out), ._4__PR1(1'b1), ._5__Q1(Q0),
    ._6__nQ1(n7474_1__6__nq1), ._7__GND(1'b0), ._14__Vcc(1'b1), ._13__CLR2(1'b1), ._12__D2(n7486_1_p3),
    ._11__CLK2(Clock_2_out), ._10__PR2(1'b1), ._9__Q2(Q1));  // open: _8__nQ2
  // _7486 7486_1: pin names not known; wires that end beside it: n7474_1__6__nq1, Q1, n7486_1_p3, 1'b0, 1'b1
endmodule

module bai3 (
  input  [2:0] Input,
  output [7:0] Output
);

  // _74138 74138_1: pin names not known; wires that end beside it: Input[0], Input[1], Input[2], 1'b0, 1'b0, 1'b1, Output[7], 1'b0, 1'b1, Output[0], Output[1], Output[2], Output[3], Output[4], Output[5], Output[6]
endmodule

module bai4 (
  input  [7:0] A,
  input  [7:0] B,
  output A_B,
  output A_B_2,
  output A_B_3
);

  wire n7485_1_yeq, n7485_1_ygt, n7485_1_ylt;

  _7485 u_7485_1 (
    .B4(B[3]), .CLT(1'b0), .CEQ(1'b1), .CGT(1'b0), .YGT(n7485_1_ygt), .YEQ(n7485_1_yeq), .YLT(n7485_1_ylt),
    .GND(1'b0), .VCC(1'b1), .A4(A[3]), .B3(B[2]), .A3(A[2]), .A2(A[1]), .B2(B[1]), .A1(A[0]), .B1(B[0]));
  _7485 u_7485_2 (
    .B4(B[7]), .CLT(n7485_1_ylt), .CEQ(n7485_1_yeq), .CGT(n7485_1_ygt), .YGT(A_B_3), .YEQ(A_B_2), .YLT(A_B),
    .GND(1'b0), .VCC(1'b1), .A4(A[7]), .B3(B[6]), .A3(A[6]), .A2(A[5]), .B2(B[5]), .A1(A[4]), .B1(B[4]));
endmodule

module ggnore (
  input  D,
  input  C,
  input  B,
  input  A,
  output JD,
  output KD,
  output JC,
  output KC,
  output JB,
  output KB,
  output JA,
  output KA
);

  wire and_3_out, and_4_out, and_6_out, not_1_out, not_2_out, not_3_out, not_4_out, not_5_out, not_6_out;

  and and_1 (JD, C, not_1_out, not_2_out);
  not not_1 (not_1_out, B);
  not not_2 (not_2_out, A);
  and and_2 (KD, C, B, not_3_out);
  not not_3 (not_3_out, A);
  and and_3 (and_3_out, B, not_4_out);
  not not_4 (not_4_out, A);
  and and_4 (and_4_out, D, not_5_out, not_6_out);
  not not_5 (not_5_out, B);
  not not_6 (not_6_out, A);
  and and_5 (KC, B, A);
  and and_6 (and_6_out, D, C);
  or or_1 (JC, and_3_out, and_4_out);
  or or_2 (KB, A, and_6_out);

  assign JA = 1'b1;
  assign JB = A;
  assign KA = 1'b1;
endmodule

module synchronos (
  input  in_1,
  output D,
  output C,
  output B,
  output A
);

  wire clock_1_out, ggnore_1_ja, ggnore_1_jb, ggnore_1_jc, ggnore_1_jd, ggnore_1_ka, ggnore_1_kb,
       ggnore_1_kc, ggnore_1_kd;

  ggnore ggnore_1 (
    .D(D), .C(C), .B(B), .A(A), .JD(ggnore_1_jd), .KD(ggnore_1_kd), .JC(ggnore_1_jc), .KC(ggnore_1_kc),
    .JB(ggnore_1_jb), .KB(ggnore_1_kb), .JA(ggnore_1_ja), .KA(ggnore_1_ka));
  Clock clock_1 (.out(clock_1_out));
  J_K_Flip_Flop j_k_ff_1 (
    .J(ggnore_1_jd), .clk(clock_1_out), .K(ggnore_1_kd), .Q(D), .preset(in_1));  // open: Qn, en, reset
  J_K_Flip_Flop j_k_ff_2 (
    .J(ggnore_1_jc), .clk(clock_1_out), .K(ggnore_1_kc), .Q(C), .reset(in_1));  // open: Qn, preset, en
  J_K_Flip_Flop j_k_ff_3 (
    .J(ggnore_1_jb), .clk(clock_1_out), .K(ggnore_1_kb), .Q(B), .preset(in_1));  // open: Qn, en, reset
  J_K_Flip_Flop j_k_ff_4 (
    .J(ggnore_1_ja), .clk(clock_1_out), .K(ggnore_1_ka), .Q(A), .preset(in_1));  // open: Qn, en, reset
endmodule

module gga (
  input  in_1
);

  wire clock_1_out, d_ff_1_q, d_ff_2_q, d_ff_3_q, re_1_da, re_1_db, re_1_dc;

  Clock clock_1 (.out(clock_1_out));
  re re_1 (.C(d_ff_1_q), .B(d_ff_2_q), .A(d_ff_3_q), .DC(re_1_dc), .DB(re_1_db), .DA(re_1_da));
  D_Flip_Flop d_ff_1 (.clk(clock_1_out), .D(re_1_dc), .Q(d_ff_1_q), .reset(in_1));  // open: Qn, preset, en
  D_Flip_Flop d_ff_2 (.clk(clock_1_out), .D(re_1_db), .Q(d_ff_2_q), .reset(in_1));  // open: Qn, preset, en
  D_Flip_Flop d_ff_3 (.clk(clock_1_out), .D(re_1_da), .Q(d_ff_3_q), .reset(in_1));  // open: Qn, preset, en
endmodule

module re (
  input  C,
  input  B,
  input  A,
  output DC,
  output DB,
  output DA
);

  wire not_1_out, not_2_out, not_3_out, not_4_out, not_5_out, not_6_out, or_1_out, or_2_out, or_3_out,
       or_4_out, or_5_out, or_6_out, or_7_out, or_8_out, or_9_out;

  or or_1 (or_1_out, C, A);
  or or_2 (or_2_out, C, B);
  or or_3 (or_3_out, B, A);
  not not_1 (not_1_out, C);
  not not_2 (not_2_out, C);
  not not_3 (not_3_out, C);
  not not_4 (not_4_out, C);
  not not_5 (not_5_out, A);
  not not_6 (not_6_out, A);
  and and_1 (DC, or_1_out, or_2_out, or_3_out);
  or or_4 (or_4_out, B, A);
  or or_5 (or_5_out, not_1_out, B);
  or or_6 (or_6_out, not_2_out, A);
  or or_7 (or_7_out, not_3_out, B);
  or or_8 (or_8_out, not_4_out, not_5_out);
  or or_9 (or_9_out, B, not_6_out);
  and and_2 (DB, or_4_out, or_5_out, or_6_out);
  and and_3 (DA, or_7_out, or_8_out, or_9_out);
endmodule

module tr (
);

  wire clock_1_out, j_k_ff_1_q, j_k_ff_2_q, j_k_ff_3_q, rt_1_ja, rt_1_jb, rt_1_jc, rt_1_ka, rt_1_kb, rt_1_kc;

  rt rt_1 (
    .C(j_k_ff_1_q), .B(j_k_ff_2_q), .A(j_k_ff_3_q), .JC(rt_1_jc), .KC(rt_1_kc), .JB(rt_1_jb), .KB(rt_1_kb),
    .JA(rt_1_ja), .KA(rt_1_ka));
  Clock clock_1 (.out(clock_1_out));
  J_K_Flip_Flop j_k_ff_1 (.J(rt_1_jc), .clk(clock_1_out), .K(rt_1_kc), .Q(j_k_ff_1_q));  // open: Qn, preset, en, reset
  J_K_Flip_Flop j_k_ff_2 (.J(rt_1_jb), .clk(clock_1_out), .K(rt_1_kb), .Q(j_k_ff_2_q));  // open: Qn, preset, en, reset
  J_K_Flip_Flop j_k_ff_3 (.J(rt_1_ja), .clk(clock_1_out), .K(rt_1_ka), .Q(j_k_ff_3_q));  // open: Qn, preset, en, reset
endmodule

module rt (
  input  C,
  input  B,
  input  A,
  output JC,
  output KC,
  output JB,
  output KB,
  output JA,
  output KA
);

  wire not_1_out, not_2_out, not_3_out, not_4_out, not_5_out, not_6_out;

  and and_1 (JC, B, A);
  not not_1 (not_1_out, B);
  not not_2 (not_2_out, A);
  not not_3 (not_3_out, C);
  not not_4 (not_4_out, A);
  not not_5 (not_5_out, C);
  not not_6 (not_6_out, B);
  and and_2 (KC, not_1_out, not_2_out);
  and and_3 (JB, not_3_out, A);
  and and_4 (KB, C, not_4_out);
  or or_1 (JA, not_5_out, B);
  or or_2 (KA, C, not_6_out);
endmodule

module lasttest (
);

  _7474 u_7474_1 ();  // open: _1__CLR1, _2__D1, _3__CLK1, _4__PR1, _5__Q1, _6__nQ1, _7__GND, _14__Vcc, _13__CLR2, _12__D2, _11__CLK2, _10__PR2, _9__Q2, _8__nQ2
endmodule

module teee (
  input  in_1,
  input  in_2
);

  wire and_1_out, and_2_out, and_3_out, and_4_out, and_5_out, clock_1_out, j_k_ff_1_q, j_k_ff_1_qn,
       j_k_ff_2_q, j_k_ff_2_qn, j_k_ff_3_q, j_k_ff_3_qn, j_k_ff_4_q, j_k_ff_4_qn, or_1_out, or_2_out;

  Clock clock_1 (.out(clock_1_out));
  and and_1 (and_1_out, j_k_ff_4_q, j_k_ff_3_q, j_k_ff_2_qn);
  J_K_Flip_Flop j_k_ff_1 (
    .J(and_1_out), .clk(clock_1_out), .K(and_2_out), .Q(j_k_ff_1_q), .Qn(j_k_ff_1_qn), .reset(in_2));  // open: preset, en
  and and_2 (and_2_out, j_k_ff_2_qn, j_k_ff_3_qn, j_k_ff_4_qn);
  and and_3 (and_3_out, j_k_ff_2_qn, j_k_ff_1_qn);
  J_K_Flip_Flop j_k_ff_2 (
    .J(or_1_out), .clk(clock_1_out), .K(and_5_out), .Q(j_k_ff_2_q), .Qn(j_k_ff_2_qn), .reset(in_2));  // open: preset, en
  or or_1 (or_1_out, and_4_out, and_5_out);
  and and_4 (and_4_out, j_k_ff_1_qn, j_k_ff_3_q, j_k_ff_4_q);
  and and_5 (and_5_out, j_k_ff_3_qn, j_k_ff_4_qn);
  J_K_Flip_Flop j_k_ff_3 (
    .J(j_k_ff_4_qn), .clk(clock_1_out), .K(or_2_out), .Q(j_k_ff_3_q), .Qn(j_k_ff_3_qn), .preset(in_2));  // open: en, reset
  or or_2 (or_2_out, j_k_ff_4_qn, and_3_out);
  J_K_Flip_Flop j_k_ff_4 (
    .J(in_1), .clk(clock_1_out), .K(in_1), .Q(j_k_ff_4_q), .Qn(j_k_ff_4_qn), .reset(in_2));  // open: preset, en
endmodule

module lastchan (
  input  in_1,
  output B,
  output A,
  output B_2,
  output A_2
);

  wire clock_1_out, clock_2_out, n7400_1_p3, n7474_1__8__nq2, n7486_1_p4;

  Clock clock_1 (.out(clock_1_out));
  _7474 u_7474_1 (
    ._1__CLR1(1'b1), ._2__D1(n7474_1__8__nq2), ._3__CLK1(clock_1_out), ._4__PR1(1'b1), ._5__Q1(A),
    ._7__GND(1'b0), ._14__Vcc(1'b1), ._13__CLR2(1'b1), ._12__D2(A), ._11__CLK2(clock_1_out), ._10__PR2(1'b1),
    ._9__Q2(B), ._8__nQ2(n7474_1__8__nq2));  // open: _6__nQ1
  Clock clock_2 (.out(clock_2_out));
  _7474 u_7474_2 (
    ._1__CLR1(in_1), ._2__D1(n7400_1_p3), ._3__CLK1(clock_2_out), ._5__Q1(A_2), ._7__GND(1'b0),
    ._14__Vcc(1'b1), ._12__D2(n7486_1_p4), ._11__CLK2(clock_2_out), ._10__PR2(in_1), ._9__Q2(B_2));  // open: _4__PR1, _6__nQ1, _13__CLR2, _8__nQ2
  // _7400 7400_1: pin names not known; wires that end beside it: A_2, B_2, n7400_1_p3, 1'b1
  // _7486 7486_1: pin names not known; wires that end beside it: 1'b0, A_2, B_2, n7486_1_p4, 1'b0, 1'b1
endmodule
