// Logisim project bai_tap_1_da_giai_bai_10.circ as structural Verilog: 1 circuit, main circuit 10
module _10 (
  input  a3,
  input  a2,
  input  a1,
  output x
);

  wire and_1_out, and_2_out;

  and and_1 (and_1_out, a3, a1);
  and and_2 (and_2_out, a3, a2);
  or or_1 (x, and_1_out, and_2_out);
endmodule
