// Logisim project bai_tap_1_da_giai_bai_8.circ as structural Verilog: 1 circuit, main circuit 8
module _8 (
  input  a,
  input  b,
  input  c,
  input  d,
  output x
);

  wire and_1_out, and_2_out;

  and and_1 (and_1_out, a, b);
  and and_2 (and_2_out, c, d, b);
  or or_1 (x, and_1_out, and_2_out);

  // Notes on the sheet:
  //   a: > 5 giờ, b: shutdiwn, c: friday, d: complete
endmodule
