// Logisim project bai_tap_1_da_giai_bai_9.circ as structural Verilog: 1 circuit, main circuit 9
module _9 (
  input  a,
  input  b,
  input  c,
  output x
);

  wire and_1_out, and_2_out, not_1_out;

  not not_1 (not_1_out, b);
  and and_1 (and_1_out, c, not_1_out);
  and and_2 (and_2_out, a, b);
  or or_1 (x, and_1_out, and_2_out);
endmodule
