// Logisim project latch_and_flip_flop.circ as structural Verilog: 24 circuits, main circuit SR Latch Active High
module SR_Latch_Active_High (
  input  R,
  input  S,
  output Q,
  output Q_prime
);

  nor nor_1 (Q, R, Q_prime);
  nor nor_2 (Q_prime, Q, S);
endmodule

module SR_Latch_Active_Low (
  input  S,
  input  R,
  output Q,
  output Q_prime
);

  nand nand_1 (Q, S, Q_prime);
  nand nand_2 (Q_prime, Q, R);
endmodule

module Gated_SR_Latch_Active_High_With_NOR (
  input  R,
  input  E,
  input  S,
  output Q,
  output Q_prime
);

  wire and_1_out, and_2_out;

  and and_1 (and_1_out, R, E);
  and and_2 (and_2_out, E, S);
  nor nor_1 (Q, and_1_out, Q_prime);
  nor nor_2 (Q_prime, Q, and_2_out);
endmodule

module Gated_SR_Latch_Active_High_With_NAND (
  input  S,
  input  E,
  input  R,
  output Q,
  output Q_prime
);

  wire nand_1_out, nand_2_out;

  nand nand_1 (nand_1_out, S, E);
  nand nand_2 (nand_2_out, E, R);
  nand nand_3 (Q, nand_1_out, Q_prime);
  nand nand_4 (Q_prime, Q, nand_2_out);
endmodule

module Gated_D_Latch_Active_High_With_NOR (
  input  E,
  input  D,
  output Q,
  output Q_prime
);

  wire and_1_out, and_2_out, not_1_out;

  not not_1 (not_1_out, D);
  and and_1 (and_1_out, not_1_out, E);
  and and_2 (and_2_out, E, D);
  nor nor_1 (Q, and_1_out, Q_prime);
  nor nor_2 (Q_prime, Q, and_2_out);
endmodule

module Gated_D_Latch_Active_High_With_NAND (
  input  D,
  input  E,
  output Q,
  output Q_prime
);

  wire nand_1_out, nand_2_out, not_1_out;

  not not_1 (not_1_out, D);
  nand nand_1 (nand_1_out, D, E);
  nand nand_2 (nand_2_out, E, not_1_out);
  nand nand_3 (Q, nand_1_out, Q_prime);
  nand nand_4 (Q_prime, Q, nand_2_out);
endmodule

module Gated_D_Latch_Active_High_With_NAND_Without_NOT (
  input  D,
  input  E,
  output Q,
  output Q_prime
);

  wire nand_1_out, nand_2_out;

  nand nand_1 (nand_1_out, D, E);
  nand nand_2 (nand_2_out, nand_1_out, E);
  nand nand_3 (Q, nand_1_out, Q_prime);
  nand nand_4 (Q_prime, Q, nand_2_out);
endmodule

module JK_Latch_Active_High_With_NOR (
  input  K,
  input  J,
  output Q,
  output Q_prime
);

  wire and_1_out, and_2_out;

  and and_1 (and_1_out, Q, K);
  and and_2 (and_2_out, J, Q_prime);
  nor nor_1 (Q, and_1_out, Q_prime);
  nor nor_2 (Q_prime, Q, and_2_out);
endmodule

module JK_Latch_Avtive_High_With_NAND (
  input  J,
  input  K,
  output Q,
  output Q_prime
);

  wire nand_1_out, nand_2_out;

  nand nand_1 (nand_1_out, Q_prime, J);
  nand nand_2 (nand_2_out, K, Q);
  nand nand_3 (Q, nand_1_out, Q_prime);
  nand nand_4 (Q_prime, Q, nand_2_out);
endmodule

module Gated_JK_Latch_Active_High (
  input  J,
  input  E,
  input  K,
  output Q,
  output Q_prime
);

  wire nand_1_out, nand_2_out;

  nand nand_1 (nand_1_out, Q_prime, J, E);
  nand nand_2 (nand_2_out, E, K, Q);
  nand nand_3 (Q, nand_1_out, Q_prime);
  nand nand_4 (Q_prime, Q, nand_2_out);
endmodule

module SR_Flip_Flop_Active_High_With_NAND (
  input  S,
  input  E,
  input  R,
  output Q,
  output Q_prime
);

  wire and_1_out, nand_1_out, nand_2_out, not_1_out;

  and and_1 (and_1_out, E, not_1_out);
  not not_1 (not_1_out, E);
  nand nand_1 (nand_1_out, S, and_1_out);
  nand nand_2 (nand_2_out, and_1_out, R);
  nand nand_3 (Q, nand_1_out, Q_prime);
  nand nand_4 (Q_prime, Q, nand_2_out);
endmodule

module D_Flip_Flop_Active_High (
  input  D,
  input  E,
  output Q,
  output Q_prime
);

  wire and_1_out, nand_1_out, nand_2_out, not_1_out;

  not not_1 (not_1_out, E);
  and and_1 (and_1_out, E, not_1_out);
  nand nand_1 (nand_1_out, D, and_1_out);
  nand nand_2 (nand_2_out, nand_1_out, and_1_out);
  nand nand_3 (Q, nand_1_out, Q_prime);
  nand nand_4 (Q_prime, Q, nand_2_out);
endmodule

module Master_Slave_D_Flip_Flop_Active_High (
  input  D,
  input  E,
  output Q,
  output Q_prime
);

  wire and_1_out, nand_1_out, nand_2_out, nand_3_out, nand_4_out, nand_5_out, nand_6_out, not_1_out,
       not_2_out;

  not not_1 (not_1_out, E);
  and and_1 (and_1_out, E, not_1_out);
  nand nand_1 (nand_1_out, D, and_1_out);
  nand nand_2 (nand_2_out, nand_1_out, and_1_out);
  not not_2 (not_2_out, and_1_out);
  nand nand_3 (nand_3_out, nand_1_out, nand_4_out);
  nand nand_4 (nand_4_out, nand_3_out, nand_2_out);
  nand nand_5 (nand_5_out, nand_3_out, not_2_out);
  nand nand_6 (nand_6_out, not_2_out, nand_4_out);
  nand nand_7 (Q, nand_5_out, Q_prime);
  nand nand_8 (Q_prime, Q, nand_6_out);
endmodule

module Master_Slave_D_Flip_Flop_Active_Low (
  input  D,
  input  E,
  output Q,
  output Q_prime
);

  wire and_1_out, and_2_out, and_3_out, nand_1_out, nand_2_out, nand_3_out, nand_4_out, not_1_out, not_2_out;

  not not_1 (not_1_out, E);
  and and_1 (and_1_out, E, not_1_out);
  nand nand_1 (nand_1_out, D, and_1_out);
  nand nand_2 (nand_2_out, nand_1_out, and_1_out);
  not not_2 (not_2_out, and_1_out);
  nand nand_3 (nand_3_out, nand_1_out, nand_4_out);
  nand nand_4 (nand_4_out, nand_3_out, nand_2_out);
  and and_2 (and_2_out, nand_3_out, not_2_out);
  and and_3 (and_3_out, not_2_out, nand_4_out);
  nor nor_1 (Q, and_2_out, Q_prime);
  nor nor_2 (Q_prime, Q, and_3_out);
endmodule

module JK_Flip_Flop_Active_High (
  input  J,
  input  E,
  input  K,
  output Q,
  output Q_prime
);

  wire and_1_out, nand_1_out, nand_2_out, not_1_out;

  and and_1 (and_1_out, E, not_1_out);
  not not_1 (not_1_out, E);
  nand nand_1 (nand_1_out, Q_prime, J, and_1_out);
  nand nand_2 (nand_2_out, and_1_out, K, Q);
  nand nand_3 (Q, nand_1_out, Q_prime);
  nand nand_4 (Q_prime, Q, nand_2_out);
endmodule

module JK_Flip_Flop_Active_High_With_Clear_And_Preset_Active_Low (
  input  Clear,
  input  J,
  input  E,
  input  K,
  input  Preset,
  output Q,
  output Q_prime
);

  wire and_1_out, nand_1_out, nand_2_out, not_1_out;

  and and_1 (and_1_out, E, not_1_out);
  not not_1 (not_1_out, E);
  nand nand_1 (nand_1_out, Q_prime, Clear, J, and_1_out);
  nand nand_2 (nand_2_out, and_1_out, K, Preset, Q);
  nand nand_3 (Q, nand_1_out, Preset, Q_prime);
  nand nand_4 (Q_prime, Q, Clear, nand_2_out);
endmodule

module T_Flip_Flop_Active_High (
  input  T,
  input  E,
  output Q,
  output Q_prime
);

  wire and_1_out, nand_1_out, nand_2_out, not_1_out;

  not not_1 (not_1_out, E);
  and and_1 (and_1_out, E, not_1_out);
  nand nand_1 (nand_1_out, Q_prime, T, and_1_out);
  nand nand_2 (nand_2_out, and_1_out, T, Q);
  nand nand_3 (Q, nand_1_out, Q_prime);
  nand nand_4 (Q_prime, Q, nand_2_out);
endmodule

module EX___OR_By_NAND (
  input  in_1,
  input  in_2,
  output out_3
);

  wire nand_1_out, nand_2_out, nand_3_out;

  nand nand_1 (nand_1_out, in_1, in_2);
  nand nand_2 (nand_2_out, in_1, nand_1_out);
  nand nand_3 (nand_3_out, nand_1_out, in_2);
  nand nand_4 (out_3, nand_2_out, nand_3_out);
endmodule

module EX___NOR_By_NOR (
  input  in_1,
  input  in_2,
  output out_3
);

  wire nor_1_out, nor_2_out, nor_3_out;

  nor nor_1 (nor_1_out, in_1, in_2);
  nor nor_2 (nor_2_out, in_1, nor_1_out);
  nor nor_3 (nor_3_out, nor_1_out, in_2);
  nor nor_4 (out_3, nor_2_out, nor_3_out);
endmodule

module test (
  output A,
  output B,
  output C,
  output D
);

  wire Clock_out, IC1_out_5, IC1_out_6, IC2_out_5, IC2_out_6, IC3_out_5, IC3_out_6, IC4_out_5, IC4_out_6;

  Clock Clock (.out(Clock_out));
  Null_IC_4_Input_2_Output IC1 (.in_1(A), .in_2(B), .in_3(C), .in_4(C), .out_5(IC1_out_5), .out_6(IC1_out_6));
  J_K_Flip_Flop j_k_ff_1 (.J(IC1_out_5), .clk(Clock_out), .K(IC1_out_6), .Q(A));  // open: Qn, preset, en, reset
  Null_IC_4_Input_2_Output IC2 (.in_1(A), .in_2(B), .in_3(C), .in_4(C), .out_5(IC2_out_5), .out_6(IC2_out_6));
  J_K_Flip_Flop j_k_ff_2 (.J(IC2_out_5), .clk(Clock_out), .K(IC2_out_6), .Q(B));  // open: Qn, preset, en, reset
  Null_IC_4_Input_2_Output IC3 (.in_1(A), .in_2(B), .in_3(C), .in_4(C), .out_5(IC3_out_5), .out_6(IC3_out_6));
  J_K_Flip_Flop j_k_ff_3 (.J(IC3_out_5), .clk(Clock_out), .K(IC3_out_6), .Q(C));  // open: Qn, preset, en, reset
  Null_IC_4_Input_2_Output IC4 (.in_1(A), .in_2(B), .in_3(C), .in_4(C), .out_5(IC4_out_5), .out_6(IC4_out_6));
  J_K_Flip_Flop j_k_ff_4 (.J(IC4_out_5), .clk(Clock_out), .K(IC4_out_6), .Q(C));  // open: Qn, preset, en, reset

  assign D = C;
endmodule

module Null_IC_4_Input_2_Output (
  input  in_1,
  input  in_2,
  input  in_3,
  input  in_4,
  output out_5,
  output out_6
);
endmodule

module IC1 (
  input  A,
  input  B,
  input  C,
  input  D,
  output K,
  output J
);

  wire not_1_out, not_2_out, not_3_out;

  not not_1 (not_1_out, B);
  not not_2 (not_2_out, C);
  not not_3 (not_3_out, D);
  and and_1 (K, not_1_out, not_2_out, not_3_out);
  and and_2 (J, not_2_out, D);
endmodule

module testvong (
  input  Start,
  output X,
  output Y,
  output Z,
  output W
);

  wire Clock_out;

  Clock Clock (.out(Clock_out));
  D_Flip_Flop d_ff_1 (.clk(Clock_out), .D(W), .Q(X), .preset(Start));  // open: Qn, en, reset
  D_Flip_Flop d_ff_2 (.clk(Clock_out), .D(X), .Q(Y), .reset(Start));  // open: Qn, preset, en
  D_Flip_Flop d_ff_3 (.clk(Clock_out), .D(Y), .Q(Z), .reset(Start));  // open: Qn, preset, en
  D_Flip_Flop d_ff_4 (.clk(Clock_out), .D(Z), .Q(W), .reset(Start));  // open: Qn, preset, en
endmodule

module testjohnson (
  input  Start,
  output X,
  output Y,
  output Z,
  output W
);

  wire Clock_out, d_ff_4_qn;

  Clock Clock (.out(Clock_out));
  D_Flip_Flop d_ff_1 (.clk(Clock_out), .D(d_ff_4_qn), .Q(X), .reset(Start));  // open: Qn, preset, en
  D_Flip_Flop d_ff_2 (.clk(Clock_out), .D(X), .Q(Y), .reset(Start));  // open: Qn, preset, en
  D_Flip_Flop d_ff_3 (.clk(Clock_out), .D(Y), .Q(Z), .reset(Start));  // open: Qn, preset, en
  D_Flip_Flop d_ff_4 (.clk(Clock_out), .D(Z), .Q(W), .Qn(d_ff_4_qn), .reset(Start));  // open: preset, en
endmodule
