// Logisim project latch_and_flip_flop_and_ic.circ as structural Verilog
module SR_Latch_Active_High (
  input  R,
  input  S,
  output Q,
  output Q_prime
);

  nor nor_1 (Q, R, Q_prime);
  nor nor_2 (Q_prime, Q, S);
endmodule

module SR_Latch_Active_Low (
  input  S,
  input  R,
  output Q,
  output Q_prime
);

  nand nand_1 (Q, S, Q_prime);
  nand nand_2 (Q_prime, Q, R);
endmodule

module Gated_SR_Latch_Active_High_With_NOR (
  input  R,
  input  E,
  input  S,
  output Q,
  output Q_prime
);

  wire and_1_out, and_2_out;

  and and_1 (and_1_out, R, E);
  and and_2 (and_2_out, E, S);
  nor nor_1 (Q, and_1_out, Q_prime);
  nor nor_2 (Q_prime, Q, and_2_out);
endmodule

module Gated_SR_Latch_Active_High_With_NAND (
  input  S,
  input  E,
  input  R,
  output Q,
  output Q_prime
);

  wire nand_1_out, nand_2_out;

  nand nand_1 (nand_1_out, S, E);
  nand nand_2 (nand_2_out, E, R);
  nand nand_3 (Q, nand_1_out, Q_prime);
  nand nand_4 (Q_prime, Q, nand_2_out);
endmodule

module Gated_D_Latch_Active_High_With_NOR (
  input  E,
  input  D,
  output Q,
  output Q_prime
);

  wire and_1_out, and_2_out, not_1_out;

  not not_1 (not_1_out, D);
  and and_1 (and_1_out, not_1_out, E);
  and and_2 (and_2_out, E, D);
  nor nor_1 (Q, and_1_out, Q_prime);
  nor nor_2 (Q_prime, Q, and_2_out);
endmodule

module Gated_D_Latch_Active_High_With_NAND (
  input  D,
  input  E,
  output Q,
  output Q_prime
);

  wire nand_1_out, nand_2_out, not_1_out;

  not not_1 (not_1_out, D);
  nand nand_1 (nand_1_out, D, E);
  nand nand_2 (nand_2_out, E, not_1_out);
  nand nand_3 (Q, nand_1_out, Q_prime);
  nand nand_4 (Q_prime, Q, nand_2_out);
endmodule

module Gated_D_Latch_Active_High_With_NAND_Without_NOT (
  input  D,
  input  E,
  output Q,
  output Q_prime
);

  wire nand_1_out, nand_2_out;

  nand nand_1 (nand_1_out, D, E);
  nand nand_2 (nand_2_out, nand_1_out, E);
  nand nand_3 (Q, nand_1_out, Q_prime);
  nand nand_4 (Q_prime, Q, nand_2_out);
endmodule

module JK_Latch_Active_High_With_NOR (
  input  K,
  input  J,
  output Q,
  output Q_prime
);

  wire and_1_out, and_2_out;

  and and_1 (and_1_out, Q, K);
  and and_2 (and_2_out, J, Q_prime);
  nor nor_1 (Q, and_1_out, Q_prime);
  nor nor_2 (Q_prime, Q, and_2_out);
endmodule

module JK_Latch_Avtive_High_With_NAND (
  input  J,
  input  K,
  output Q,
  output Q_prime
);

  wire nand_1_out, nand_2_out;

  nand nand_1 (nand_1_out, Q_prime, J);
  nand nand_2 (nand_2_out, K, Q);
  nand nand_3 (Q, nand_1_out, Q_prime);
  nand nand_4 (Q_prime, Q, nand_2_out);
endmodule

module Gated_JK_Latch_Active_High (
  input  J,
  input  E,
  input  K,
  output Q,
  output Q_prime
);

  wire nand_1_out, nand_2_out;

  nand nand_1 (nand_1_out, Q_prime, J, E);
  nand nand_2 (nand_2_out, E, K, Q);
  nand nand_3 (Q, nand_1_out, Q_prime);
  nand nand_4 (Q_prime, Q, nand_2_out);
endmodule

module SR_Flip_Flop_Active_High_With_NAND (
  input  S,
  input  E,
  input  R,
  output Q,
  output Q_prime
);

  wire and_1_out, nand_1_out, nand_2_out, not_1_out;

  and and_1 (and_1_out, E, not_1_out);
  not not_1 (not_1_out, E);
  nand nand_1 (nand_1_out, S, and_1_out);
  nand nand_2 (nand_2_out, and_1_out, R);
  nand nand_3 (Q, nand_1_out, Q_prime);
  nand nand_4 (Q_prime, Q, nand_2_out);
endmodule

module D_Flip_Flop_Active_High (
  input  D,
  input  E,
  output Q,
  output Q_prime
);

  wire and_1_out, nand_1_out, nand_2_out, not_1_out;

  not not_1 (not_1_out, E);
  and and_1 (and_1_out, E, not_1_out);
  nand nand_1 (nand_1_out, D, and_1_out);
  nand nand_2 (nand_2_out, nand_1_out, and_1_out);
  nand nand_3 (Q, nand_1_out, Q_prime);
  nand nand_4 (Q_prime, Q, nand_2_out);
endmodule

module Master_Slave_D_Flip_Flop_Active_High (
  input  D,
  input  E,
  output Q,
  output Q_prime
);

  wire and_1_out, nand_1_out, nand_2_out, nand_3_out, nand_4_out, nand_5_out, nand_6_out, not_1_out,
       not_2_out;

  not not_1 (not_1_out, E);
  and and_1 (and_1_out, E, not_1_out);
  nand nand_1 (nand_1_out, D, and_1_out);
  nand nand_2 (nand_2_out, nand_1_out, and_1_out);
  not not_2 (not_2_out, and_1_out);
  nand nand_3 (nand_3_out, nand_1_out, nand_4_out);
  nand nand_4 (nand_4_out, nand_3_out, nand_2_out);
  nand nand_5 (nand_5_out, nand_3_out, not_2_out);
  nand nand_6 (nand_6_out, not_2_out, nand_4_out);
  nand nand_7 (Q, nand_5_out, Q_prime);
  nand nand_8 (Q_prime, Q, nand_6_out);
endmodule

module Master_Slave_D_Flip_Flop_Active_Low (
  input  D,
  input  E,
  output Q,
  output Q_prime
);

  wire and_1_out, and_2_out, and_3_out, nand_1_out, nand_2_out, nand_3_out, nand_4_out, not_1_out, not_2_out;

  not not_1 (not_1_out, E);
  and and_1 (and_1_out, E, not_1_out);
  nand nand_1 (nand_1_out, D, and_1_out);
  nand nand_2 (nand_2_out, nand_1_out, and_1_out);
  not not_2 (not_2_out, and_1_out);
  nand nand_3 (nand_3_out, nand_1_out, nand_4_out);
  nand nand_4 (nand_4_out, nand_3_out, nand_2_out);
  and and_2 (and_2_out, nand_3_out, not_2_out);
  and and_3 (and_3_out, not_2_out, nand_4_out);
  nor nor_1 (Q, and_2_out, Q_prime);
  nor nor_2 (Q_prime, Q, and_3_out);
endmodule

module JK_Flip_Flop_Active_High (
  input  J,
  input  E,
  input  K,
  output Q,
  output Q_prime
);

  wire and_1_out, nand_1_out, nand_2_out, not_1_out;

  and and_1 (and_1_out, E, not_1_out);
  not not_1 (not_1_out, E);
  nand nand_1 (nand_1_out, Q_prime, J, and_1_out);
  nand nand_2 (nand_2_out, and_1_out, K, Q);
  nand nand_3 (Q, nand_1_out, Q_prime);
  nand nand_4 (Q_prime, Q, nand_2_out);
endmodule

module JK_Flip_Flop_Active_High_With_Clear_And_Preset_Active_Low (
  input  Clear,
  input  J,
  input  E,
  input  K,
  input  Preset,
  output Q,
  output Q_prime
);

  wire and_1_out, nand_1_out, nand_2_out, not_1_out;

  and and_1 (and_1_out, E, not_1_out);
  not not_1 (not_1_out, E);
  nand nand_1 (nand_1_out, Q_prime, Clear, J, and_1_out);
  nand nand_2 (nand_2_out, and_1_out, K, Preset, Q);
  nand nand_3 (Q, nand_1_out, Preset, Q_prime);
  nand nand_4 (Q_prime, Q, Clear, nand_2_out);
endmodule

module T_Flip_Flop_Active_High (
  input  T,
  input  E,
  output Q,
  output Q_prime
);

  wire and_1_out, nand_1_out, nand_2_out, not_1_out;

  not not_1 (not_1_out, E);
  and and_1 (and_1_out, E, not_1_out);
  nand nand_1 (nand_1_out, Q_prime, T, and_1_out);
  nand nand_2 (nand_2_out, and_1_out, T, Q);
  nand nand_3 (Q, nand_1_out, Q_prime);
  nand nand_4 (Q_prime, Q, nand_2_out);
endmodule

module EX___OR_By_NAND (
  input  in_1,
  input  in_2,
  output out_3
);

  wire nand_1_out, nand_2_out, nand_3_out;

  nand nand_1 (nand_1_out, in_1, in_2);
  nand nand_2 (nand_2_out, in_1, nand_1_out);
  nand nand_3 (nand_3_out, nand_1_out, in_2);
  nand nand_4 (out_3, nand_2_out, nand_3_out);
endmodule

module EX___NOR_By_NOR (
  input  in_1,
  input  in_2,
  output out_3
);

  wire nor_1_out, nor_2_out, nor_3_out;

  nor nor_1 (nor_1_out, in_1, in_2);
  nor nor_2 (nor_2_out, in_1, nor_1_out);
  nor nor_3 (nor_3_out, nor_1_out, in_2);
  nor nor_4 (out_3, nor_2_out, nor_3_out);
endmodule

module A____B___C___D__By_NAND (
  input  C,
  input  A,
  input  B,
  input  D,
  output X
);

  wire nand_1_out, nand_2_out, nand_3_out;

  nand nand_1 (nand_1_out, A, B);
  nand nand_2 (nand_2_out, C, nand_1_out);
  nand nand_3 (nand_3_out, nand_1_out, D);
  nand nand_4 (X, nand_2_out, nand_3_out);
endmodule

module A_B____CD_By_NOR (
  input  C,
  input  A,
  input  B,
  input  D,
  output X
);

  wire nor_1_out, nor_2_out, nor_3_out;

  nor nor_1 (nor_1_out, A, B);
  nor nor_2 (nor_2_out, C, nor_1_out);
  nor nor_3 (nor_3_out, nor_1_out, D);
  nor nor_4 (X, nor_2_out, nor_3_out);
endmodule

module IC_74293 (
  input  VCC,
  input  R01,
  input  R02,
  output QA,
  output QB,
  output QC,
  output QD
);

  wire Clock_A_out, Clock_B_out, nand_1_out, not_1_out, not_2_out, not_3_out, not_4_out, not_5_out, not_6_out;

  Clock Clock_A (.out(Clock_A_out));
  Clock Clock_B (.out(Clock_B_out));
  not not_1 (not_1_out, Clock_A_out);
  not not_2 (not_2_out, VCC);
  nand nand_1 (nand_1_out, R01, R02);
  J_K_Flip_Flop j_k_ff_1 (
    .J(VCC), .clk(not_1_out), .K(VCC), .Q(QA), .preset(not_2_out), .reset(not_3_out));  // open: Qn, en
  not not_3 (not_3_out, nand_1_out);
  not not_4 (not_4_out, Clock_B_out);
  J_K_Flip_Flop j_k_ff_2 (
    .J(VCC), .clk(not_4_out), .K(VCC), .Q(QB), .preset(not_2_out), .reset(not_3_out));  // open: Qn, en
  J_K_Flip_Flop j_k_ff_3 (
    .J(VCC), .clk(not_5_out), .K(VCC), .Q(QC), .preset(not_2_out), .reset(not_3_out));  // open: Qn, en
  not not_5 (not_5_out, QB);
  not not_6 (not_6_out, QC);
  J_K_Flip_Flop j_k_ff_4 (
    .J(VCC), .clk(not_6_out), .K(VCC), .Q(QD), .preset(not_2_out), .reset(not_3_out));  // open: Qn, en
endmodule

module Ring_Counter (
  input  in_1,
  output out_2,
  output out_3,
  output out_4,
  output out_5
);

  wire clock_1_out;

  Clock clock_1 (.out(clock_1_out));
  D_Flip_Flop #(.trigger("high")) d_ff_1 (
    .clk(clock_1_out), .D(out_5), .Q(out_2), .preset(in_1));  // open: Qn, en, reset
  D_Flip_Flop #(.trigger("high")) d_ff_2 (
    .clk(clock_1_out), .D(out_2), .Q(out_3), .reset(in_1));  // open: Qn, preset, en
  D_Flip_Flop #(.trigger("high")) d_ff_3 (
    .clk(clock_1_out), .D(out_3), .Q(out_4), .reset(in_1));  // open: Qn, preset, en
  D_Flip_Flop #(.trigger("high")) d_ff_4 (
    .clk(clock_1_out), .D(out_4), .Q(out_5), .reset(in_1));  // open: Qn, preset, en
endmodule

module test (
  input  Input_1,
  input  Input_2,
  output Output
);

  // _7400 7400_1: pin names not known; wires that end beside it: Input_1, Input_2, Output, 1'b0, 1'b1
endmodule

module test1 (
  input  A,
  input  B,
  input  C,
  input  A_2,
  input  B_2,
  input  C_2,
  output X,
  output Y
);

  wire and_1_out, not_1_out, not_2_out, or_2_out;

  and and_1 (and_1_out, A, B);
  not not_1 (not_1_out, C);
  not not_2 (not_2_out, C_2);
  or or_1 (X, and_1_out, not_1_out);
  or or_2 (or_2_out, A_2, B_2);
  and and_2 (Y, or_2_out, not_2_out);
endmodule

module test2 (
  input  A,
  input  B,
  input  C,
  input  A_2,
  input  B_2,
  input  C_2,
  output Y,
  output X
);

  wire n7404_1_p3, n7404_2_p3, n7408_1_p3, n7432_2_p3;

  // _7408 7408_1: pin names not known; wires that end beside it: A_2, B_2, n7408_1_p3, 1'b1
  // _7404 7404_1: pin names not known; wires that end beside it: 1'b0, C_2, n7404_1_p3, 1'b0, 1'b1
  // _7432 7432_1: pin names not known; wires that end beside it: n7408_1_p3, n7404_1_p3, X, 1'b0, 1'b1
  // _7432 7432_2: pin names not known; wires that end beside it: A, B, n7432_2_p3, 1'b1
  // _7404 7404_2: pin names not known; wires that end beside it: 1'b0, C, n7404_2_p3, 1'b0, 1'b1
  // _7408 7408_2: pin names not known; wires that end beside it: n7432_2_p3, n7404_2_p3, Y, 1'b0, 1'b1
endmodule

module test3 (
  input  M,
  input  N,
  input  P,
  input  A,
  input  B,
  output Z,
  output W
);

  wire not_1_out, not_2_out, not_3_out, or_1_out, or_2_out, or_3_out;

  or or_1 (or_1_out, M, N);
  not not_1 (not_1_out, M);
  not not_2 (not_2_out, N);
  not not_3 (not_3_out, P);
  or or_2 (or_2_out, not_1_out, P);
  or or_3 (or_3_out, not_2_out, not_3_out);
  and and_1 (Z, or_2_out, or_1_out, or_3_out);
  or or_4 (W, A, B);
endmodule

module test4 (
  input  M,
  input  N,
  input  P,
  output Z
);

  wire not_1_out, not_2_out, not_3_out, or_1_out, or_2_out, or_3_out;

  or or_1 (or_1_out, M, N);
  not not_1 (not_1_out, M);
  not not_2 (not_2_out, N);
  not not_3 (not_3_out, P);
  or or_2 (or_2_out, not_1_out, P);
  or or_3 (or_3_out, not_2_out, not_3_out);
  and and_1 (Z, or_2_out, or_1_out, or_3_out);
endmodule

module ga (
  input  M,
  input  N,
  input  P,
  input  A,
  input  B,
  output Z,
  output W
);

  wire n7408_1_p3, n7432_1_p3, n7432_1_p4, n7432_1_p6, n7432_1_p9, n7432_1_p10, n7432_1_p11;

  // _7432 7432_1: pin names not known; wires that end beside it: M, N, n7432_1_p3, n7432_1_p4, P, n7432_1_p6, 1'b0, 1'b1, n7432_1_p9, n7432_1_p10, n7432_1_p11
  // _7432 7432_2: pin names not known; wires that end beside it: A, B, W, 1'b0, 1'b1
  // _7404 7404_1: pin names not known; wires that end beside it: M, n7432_1_p4, N, n7432_1_p9, P, n7432_1_p10, 1'b0, 1'b1
  // _7408 7408_1: pin names not known; wires that end beside it: n7432_1_p3, n7432_1_p6, n7408_1_p3, n7408_1_p3, n7432_1_p11, Z, 1'b0, 1'b1
endmodule

module teste (
  output Output,
  output Output_2
);

  wire Input_2_2_out, Input_2_out;

  Clock Input_2 (.out(Input_2_out));
  // _7408 7408_1: pin names not known; wires that end beside it: 1'b1, Input_2_out, Output, 1'b0, 1'b1
  Clock Input_2_2 (.out(Input_2_2_out));
  // _7432 7432_1: pin names not known; wires that end beside it: 1'b1, Input_2_2_out, Output_2, 1'b0, 1'b1

  // Notes on the sheet:
  //   Input 1
  //   Input 1
endmodule

module gaga (
  output Output
);

  wire Input_out, not_1_out, not_2_out, not_3_out, not_4_out;

  Clock Input (.out(Input_out));
  not not_1 (not_1_out, Input_out);
  not not_2 (not_2_out, not_1_out);
  not not_3 (not_3_out, not_2_out);
  // NOT_Gate not_4 has open pins: in=open, out=not_4_out
  or or_1 (Output, Input_out, not_3_out);
  // AND_Gate and_1 has open pins: in1=not_4_out, out=open

  // Notes on the sheet:
  //   Delayed Input
endmodule

module cgag (
  output Output,
  output Output_2
);

  wire Input_2_out, Input_out, n7404_1_p2, n7404_1_p4, n7404_1_p6, n7404_2_p2, n7404_2_p4, n7404_2_p6;

  Clock Input (.out(Input_out));
  // _7404 7404_1: pin names not known; wires that end beside it: Input_out, n7404_1_p2, n7404_1_p2, n7404_1_p4, n7404_1_p4, n7404_1_p6, 1'b0, 1'b1, 1'b0
  // _7408 7408_1: pin names not known; wires that end beside it: Input_out, n7404_1_p6, Output, 1'b1
  Clock Input_2 (.out(Input_2_out));
  // _7404 7404_2: pin names not known; wires that end beside it: Input_2_out, n7404_2_p2, n7404_2_p2, n7404_2_p4, n7404_2_p4, n7404_2_p6, 1'b0, 1'b1, 1'b0
  // _7432 7432_1: pin names not known; wires that end beside it: Input_2_out, n7404_2_p6, Output_2, 1'b1
endmodule

module te (
  input  in_1,
  input  in_2,
  output out_3
);

  wire and_1_out, not_1_out;

  Clock clock_1 (.out(in_1));
  not not_1 (not_1_out, in_1);
  and and_1 (and_1_out, in_1, not_1_out);
  D_Flip_Flop #(.trigger("high")) d_ff_1 (.clk(and_1_out), .D(in_2), .Q(out_3));  // open: Qn, preset, en, reset
endmodule
